// Logisim project 1708E-R1.circ as structural Verilog
module CPU (
  input  in_1,
  input  [2:0] in_2,
  input  in_3,
  input  in_4,
  input  in_5,
  input  in_6,
  input  in_7,
  input  in_8,
  input  in_9,
  input  in_10,
  input  in_11,
  input  in_12,
  input  in_13,
  input  in_14,
  input  in_15,
  input  in_16,
  input  in_17,
  input  in_18,
  input  in_19,
  input  in_20,
  input  in_21,
  input  in_22,
  input  in_23,
  input  in_24,
  input  in_25,
  input  in_26,
  input  in_27,
  input  in_28,
  input  in_29,
  input  in_30,
  input  in_31,
  input  in_32,
  input  in_33,
  input  in_34,
  input  in_35,
  input  in_36,
  input  in_37,
  input  in_38,
  input  in_39,
  input  in_40,
  input  [7:0] From_Data_Bus,
  output [15:0] To_Address_Bus,
  output [7:0] To_Data_Bus
);

  wire ADDR0HR, ADDR0HW, ADDR0LR, ADDR0LW, ADDR1HR, ADDR1HW, ADDR1LR, ADDR1LW, AREGS, Clock, DBUS_EN, IPHR,
       IPHW, IPLR, IPLW, MRR, MRW, not_19_out, not_20_out, not_21_out, not_39_out, not_40_out, not_41_out,
       R0R, R0W, R1R, R1W, R2R, R2W, R3R, R3W, R4R, R4W, R5R, R5W, R6R, R6W, R7R, R7W, SPR, SPW, SREGS, SRR,
       SRW, WREGS;
  wire [7:0] ADDR0H, ADDR0L, ADDR1H, ADDR1L, Address_Registers_register_data_bus_2, controlled_buffer_2_out,
       controlled_buffer_4_out, controlled_buffer_6_out, controlled_buffer_7_out, CPU_BUS, IPH, IPL,
       MASK_BUS, MR, n74245_octal_bus_transceiver_3s_1_out_20, R0, R1, R2, R3, R4, R5, R6, R7, SP,
       Special_Registers_register_data_bus_2, SR, TICK0, TICK1, TICK2, TICK3, TICK4, TICK5, TICK6,
       Work_Registers_register_data_bus_2;

  not not_1 (R0W, in_3);
  not not_2 (R1W, in_5);
  not not_3 (R2W, in_7);
  not not_4 (R3W, in_9);
  not not_5 (R4W, in_11);
  not not_6 (R5W, in_13);
  not not_7 (R6W, in_15);
  not not_8 (R7W, in_17);
  not not_9 (IPHW, in_19);
  not not_10 (IPLW, in_21);
  not not_11 (ADDR0HW, in_23);
  not not_12 (ADDR0LW, in_25);
  not not_13 (ADDR1HW, in_27);
  not not_14 (ADDR1LW, in_29);
  not not_15 (SPW, in_31);
  not not_16 (SRW, in_33);
  not not_17 (MRW, in_35);
  not not_18 (DBUS_EN, in_40);
  Clock clock_1 (.out(Clock));
  not not_19 (not_19_out, in_37);
  not not_20 (not_20_out, in_38);
  not not_21 (not_21_out, in_39);
  assign CPU_BUS = not_21_out ? n74245_octal_bus_transceiver_3s_1_out_20 : 8'bz;  // Controlled_Buffer controlled_buffer_1
  not not_22 (R0R, in_4);
  not not_23 (R1R, in_6);
  not not_24 (R2R, in_8);
  not not_25 (R3R, in_10);
  not not_26 (R4R, in_12);
  not not_27 (R5R, in_14);
  not not_28 (R6R, in_16);
  not not_29 (R7R, in_18);
  not not_30 (IPHR, in_20);
  not not_31 (IPLR, in_22);
  not not_32 (ADDR0HR, in_24);
  not not_33 (ADDR0LR, in_26);
  not not_34 (ADDR1HR, in_28);
  not not_35 (ADDR1LR, in_30);
  not not_36 (SPR, in_32);
  not not_37 (SRR, in_34);
  not not_38 (MRR, in_36);
  _74373_Octal_D_Latch_3S _74373 (
    ._1D(CPU_BUS[0]), ._2D(CPU_BUS[1]), ._3D(CPU_BUS[2]), ._4D(CPU_BUS[3]), ._5D(CPU_BUS[4]),
    ._6D(CPU_BUS[5]), ._7D(CPU_BUS[6]), ._8D(CPU_BUS[7]), .Load_data_when_1(in_37),
    .Output_enabled_when_0(not_19_out), ._1Q(To_Address_Bus[8]), ._2Q(To_Address_Bus[9]),
    ._3Q(To_Address_Bus[10]), ._4Q(To_Address_Bus[11]), ._5Q(To_Address_Bus[12]), ._6Q(To_Address_Bus[13]),
    ._7Q(To_Address_Bus[14]), ._8Q(To_Address_Bus[15]));
  _74373_Octal_D_Latch_3S _74373_2 (
    ._1D(CPU_BUS[0]), ._2D(CPU_BUS[1]), ._3D(CPU_BUS[2]), ._4D(CPU_BUS[3]), ._5D(CPU_BUS[4]),
    ._6D(CPU_BUS[5]), ._7D(CPU_BUS[6]), ._8D(CPU_BUS[7]), .Load_data_when_1(in_38),
    .Output_enabled_when_0(not_20_out), ._1Q(To_Address_Bus[0]), ._2Q(To_Address_Bus[1]),
    ._3Q(To_Address_Bus[2]), ._4Q(To_Address_Bus[3]), ._5Q(To_Address_Bus[4]), ._6Q(To_Address_Bus[5]),
    ._7Q(To_Address_Bus[6]), ._8Q(To_Address_Bus[7]));
  assign controlled_buffer_2_out = in_39 ? CPU_BUS : 8'bz;  // Controlled_Buffer controlled_buffer_2
  nand nand_1 (WREGS, R0W, R1W, R2W, R3W, R4W, R5W, R6W, R7W);
  nand nand_2 (AREGS, IPHW, IPLW, ADDR0HW, ADDR0LW, ADDR1HW, ADDR1LW);
  nand nand_3 (SREGS, SPW, SRW, MRW);
  _74245_Octal_Bus_Transceiver_3S u_74245_octal_bus_transceiver_3s_1 (
    .A0(controlled_buffer_2_out[0]), .out_20(n74245_octal_bus_transceiver_3s_1_out_20[0]),
    .A1(controlled_buffer_2_out[1]), .out_22(n74245_octal_bus_transceiver_3s_1_out_20[1]),
    .A2(controlled_buffer_2_out[2]), .out_24(n74245_octal_bus_transceiver_3s_1_out_20[2]),
    .A3(controlled_buffer_2_out[3]), .out_26(n74245_octal_bus_transceiver_3s_1_out_20[3]),
    .A4(controlled_buffer_2_out[4]), .out_28(n74245_octal_bus_transceiver_3s_1_out_20[4]),
    .A5(controlled_buffer_2_out[5]), .out_30(n74245_octal_bus_transceiver_3s_1_out_20[5]),
    .A6(controlled_buffer_2_out[6]), .out_32(n74245_octal_bus_transceiver_3s_1_out_20[6]),
    .A7(controlled_buffer_2_out[7]), .out_34(n74245_octal_bus_transceiver_3s_1_out_20[7]), .DIR(in_39),
    .out_19(To_Data_Bus[0]), .B0(From_Data_Bus[0]), .out_21(To_Data_Bus[1]), .B1(From_Data_Bus[1]),
    .out_23(To_Data_Bus[2]), .B2(From_Data_Bus[2]), .out_25(To_Data_Bus[3]), .B3(From_Data_Bus[3]),
    .out_27(To_Data_Bus[4]), .B4(From_Data_Bus[4]), .out_29(To_Data_Bus[5]), .B5(From_Data_Bus[5]),
    .out_31(To_Data_Bus[6]), .B6(From_Data_Bus[6]), .out_33(To_Data_Bus[7]), .B7(From_Data_Bus[7]),
    .OE(DBUS_EN));
  Hex_Digit_Display hex_digit_display_1 (.value(R0[7:4]));  // open: dp
  Hex_Digit_Display hex_digit_display_2 (.value(R0[3:0]));  // open: dp
  Hex_Digit_Display hex_digit_display_3 (.value(R4[7:4]));  // open: dp
  Hex_Digit_Display hex_digit_display_4 (.value(R4[3:0]));  // open: dp
  Hex_Digit_Display hex_digit_display_5 (.value(ADDR0H[7:4]));  // open: dp
  Hex_Digit_Display hex_digit_display_6 (.value(ADDR0H[3:0]));  // open: dp
  Pull_Resistor pull_resistor_1 (.node(MASK_BUS[7]));
  Pull_Resistor pull_resistor_2 (.node(MASK_BUS[6]));
  Pull_Resistor pull_resistor_3 (.node(MASK_BUS[5]));
  Pull_Resistor pull_resistor_4 (.node(MASK_BUS[2]));
  Hex_Digit_Display hex_digit_display_7 (.value(R1[7:4]));  // open: dp
  Hex_Digit_Display hex_digit_display_8 (.value(R1[3:0]));  // open: dp
  Hex_Digit_Display hex_digit_display_9 (.value(R5[7:4]));  // open: dp
  Hex_Digit_Display hex_digit_display_10 (.value(R5[3:0]));  // open: dp
  Hex_Digit_Display hex_digit_display_11 (.value(ADDR0L[3:0]));  // open: dp
  Hex_Digit_Display hex_digit_display_12 (.value(ADDR0L[7:4]));  // open: dp
  Hex_Digit_Display hex_digit_display_13 (.value(R2[7:4]));  // open: dp
  Hex_Digit_Display hex_digit_display_14 (.value(R2[3:0]));  // open: dp
  Hex_Digit_Display hex_digit_display_15 (.value(R6[7:4]));  // open: dp
  Hex_Digit_Display hex_digit_display_16 (.value(R6[3:0]));  // open: dp
  Hex_Digit_Display hex_digit_display_17 (.value(ADDR1H[7:4]));  // open: dp
  Hex_Digit_Display hex_digit_display_18 (.value(ADDR1H[3:0]));  // open: dp
  Hex_Digit_Display hex_digit_display_19 (.value(R3[3:0]));  // open: dp
  Hex_Digit_Display hex_digit_display_20 (.value(R3[7:4]));  // open: dp
  Hex_Digit_Display hex_digit_display_21 (.value(R7[7:4]));  // open: dp
  Hex_Digit_Display hex_digit_display_22 (.value(R7[3:0]));  // open: dp
  Hex_Digit_Display hex_digit_display_23 (.value(ADDR1L[3:0]));  // open: dp
  Hex_Digit_Display hex_digit_display_24 (.value(ADDR1L[7:4]));  // open: dp
  Working_Registers Work_Registers (
    .R0_WE(R0W), .R0_OE(R0R), .R1_WE(R1W), .R1_OE(R1R), .R2_WE(R2W), .R2_OE(R2R), .R3_WE(R3W), .R3_OE(R3R),
    .R4_WE(R4W), .R4_OE(R4R), .R5_WE(R5W), .R5_OE(R5R), .R6_WE(R6W), .R6_OE(R6R), .R7_WE(R7W), .R7_OE(R7R),
    .Clock(Clock), .R0_Content(R0), .R1_Content(R1), .R2_Content(R2), .R3_Content(R3),
    .Register_Data_Bus(controlled_buffer_4_out), .Register_Data_Bus_2(Work_Registers_register_data_bus_2),
    .R4_Content(R4), .R5_Content(R5), .R6_Content(R6), .R7_Content(R7));
  not not_39 (not_39_out, WREGS);
  assign CPU_BUS = not_39_out ? Work_Registers_register_data_bus_2 : 8'bz;  // Controlled_Buffer controlled_buffer_3
  Hex_Digit_Display hex_digit_display_25 (.value(TICK6[3:0]));  // open: dp
  Hex_Digit_Display hex_digit_display_26 (.value(TICK6[7:4]));  // open: dp
  Hex_Digit_Display hex_digit_display_27 (.value(SP[7:4]));  // open: dp
  Hex_Digit_Display hex_digit_display_28 (.value(SP[3:0]));  // open: dp
  Hex_Digit_Display hex_digit_display_29 (.value(IPH[7:4]));  // open: dp
  Hex_Digit_Display hex_digit_display_30 (.value(IPH[3:0]));  // open: dp
  assign controlled_buffer_4_out = WREGS ? CPU_BUS : 8'bz;  // Controlled_Buffer controlled_buffer_4
  ROM rom_1 ();  // open: addr, data, sel
  Hex_Digit_Display hex_digit_display_31 (.value(TICK5[7:4]));  // open: dp
  Hex_Digit_Display hex_digit_display_32 (.value(TICK5[3:0]));  // open: dp
  Hex_Digit_Display hex_digit_display_33 (.value(SR[3:0]));  // open: dp
  Hex_Digit_Display hex_digit_display_34 (.value(SR[7:4]));  // open: dp
  Hex_Digit_Display hex_digit_display_35 (.value(IPL[3:0]));  // open: dp
  Hex_Digit_Display hex_digit_display_36 (.value(IPL[7:4]));  // open: dp
  Hex_Digit_Display hex_digit_display_37 (.value(TICK4[3:0]));  // open: dp
  Hex_Digit_Display hex_digit_display_38 (.value(TICK4[7:4]));  // open: dp
  Hex_Digit_Display hex_digit_display_39 (.value(MR[3:0]));  // open: dp
  Hex_Digit_Display hex_digit_display_40 (.value(MR[7:4]));  // open: dp
  Tick_Register tick_register_1 (
    .Byte_Select_0(in_2[0]), .Read(in_1), .Falling_edge_triggered_clock(Clock), .out_6(CPU_BUS),
    .Byte_0(TICK0), .Byte_1(TICK1), .Byte_2(TICK2), .Byte_3(TICK3), .Byte_4(TICK4), .Byte_5(TICK5),
    .Byte_6(TICK6), .Byte_Select_1(in_2[1]), .Byte_Select_2(in_2[2]));
  Hex_Digit_Display hex_digit_display_41 (.value(TICK3[7:4]));  // open: dp
  Hex_Digit_Display hex_digit_display_42 (.value(TICK3[3:0]));  // open: dp
  Hex_Digit_Display hex_digit_display_43 (.value(TICK2[7:4]));  // open: dp
  Hex_Digit_Display hex_digit_display_44 (.value(TICK2[3:0]));  // open: dp
  Hex_Digit_Display hex_digit_display_45 (.value(TICK1[7:4]));  // open: dp
  Hex_Digit_Display hex_digit_display_46 (.value(TICK1[3:0]));  // open: dp
  Address_Registers Address_Registers (
    .ADDR0H_WE(ADDR0HW), .ADDR0H_OE(ADDR0HR), .ADDR0L_WE(ADDR0LW), .ADDR0L_OE(ADDR0LR), .ADDR1H_WE(ADDR1HW),
    .ADDR1H_OE(ADDR1HR), .ADDR1L_WE(ADDR1LW), .ADDR1L_OE(ADDR1LR), .IPH_WE(IPHW), .IPH_OE(IPHR),
    .IPL_WE(IPLW), .IPL_OE(IPLR), .Register_Data_Bus(controlled_buffer_6_out), .Clock(Clock),
    .Register_Data_Bus_2(Address_Registers_register_data_bus_2), .ADDR0H_Content(ADDR0H), .IPH_Content(IPH),
    .ADDR0L_Content(ADDR0L), .IPL_Content(IPL), .ADDR1H_Content(ADDR1H), .ADDR1L_Content(ADDR1L));
  not not_40 (not_40_out, AREGS);
  assign CPU_BUS = not_40_out ? Address_Registers_register_data_bus_2 : 8'bz;  // Controlled_Buffer controlled_buffer_5
  Hex_Digit_Display hex_digit_display_47 (.value(TICK0[3:0]));  // open: dp
  Hex_Digit_Display hex_digit_display_48 (.value(TICK0[7:4]));  // open: dp
  assign controlled_buffer_6_out = AREGS ? CPU_BUS : 8'bz;  // Controlled_Buffer controlled_buffer_6
  Special_Registers Special_Registers (
    .SP_WE(SPW), .SP_OE(SPR), .SR_WE(SRW), .SR_OE(SRR), .Register_Data_Bus(controlled_buffer_7_out),
    .Masking_Bus(MASK_BUS), .Clock(Clock), .Register_Data_Bus_2(Special_Registers_register_data_bus_2),
    .SP_Content(SP), .SB_Content(SR), .MR_Content(MR), .MR_WE(MRW), .MR_OE(MRR));
  not not_41 (not_41_out, SREGS);
  assign controlled_buffer_7_out = SREGS ? CPU_BUS : 8'bz;  // Controlled_Buffer controlled_buffer_7
  assign CPU_BUS = not_41_out ? Special_Registers_register_data_bus_2 : 8'bz;  // Controlled_Buffer controlled_buffer_8

  // Other names for the same wires on the sheet: ADDRHW = in_37; ADDRLW = in_38; DBUS_RW = in_39; TICK = in_1;
  //   TickSelect[2:0] = in_2

  // Notes on the sheet:
  //   Address Bus Interface
  //   Bus I/O 3-State Emulation
  //   Bus 3-State I/O Emulation Helper
  //   Data Bus Interface
  //   Avoid floating lines
  //   Bus I/O 3-State Emulation
  //   Microcode Decoder ROM
  //   Bus I/O 3-State Emulation
  //   Bus I/O 3-State Emulation
endmodule

// WREGS
module Working_Registers (
  input  R0_WE,
  input  R0_OE,
  input  R1_WE,
  input  R1_OE,
  input  R2_WE,
  input  R2_OE,
  input  R3_WE,
  input  R3_OE,
  input  R4_WE,
  input  R4_OE,
  input  R5_WE,
  input  R5_OE,
  input  R6_WE,
  input  R6_OE,
  input  [7:0] Register_Data_Bus,
  input  R7_WE,
  input  R7_OE,
  input  Clock,
  output [7:0] Register_Data_Bus_2,
  output [7:0] R0_Content,
  output [7:0] R1_Content,
  output [7:0] R2_Content,
  output [7:0] R3_Content,
  output [7:0] R4_Content,
  output [7:0] R5_Content,
  output [7:0] R6_Content,
  output [7:0] R7_Content
);

  wire and_1_out, nand_1_out, nand_2_out, not_1_out, not_2_out, not_3_out, not_4_out, not_5_out, not_6_out,
       not_7_out, not_8_out, not_9_out, not_10_out, not_11_out, not_12_out, not_13_out, not_14_out,
       not_15_out, not_16_out, pull_resistor_1_node, pull_resistor_2_node, pull_resistor_3_node,
       pull_resistor_4_node, pull_resistor_5_node, pull_resistor_6_node, pull_resistor_7_node,
       pull_resistor_8_node;
  wire [7:0] controlled_buffer_1_out, R0_output, R1_output, R2_output, R3_output, R4_output, R5_output,
       R6_output, R7_output;

  and and_1 (and_1_out, ~nand_2_out, nand_1_out);  // AND_Gate
  assign controlled_buffer_1_out = and_1_out ? Register_Data_Bus : 8'bz;  // Controlled_Buffer controlled_buffer_1
  assign Register_Data_Bus_2 = nand_2_out ? controlled_buffer_1_out : 8'bz;  // Controlled_Buffer controlled_buffer_2
  Pull_Resistor #(.pull(1)) pull_resistor_1 (.node(pull_resistor_1_node));
  Pull_Resistor #(.pull(1)) pull_resistor_2 (.node(pull_resistor_2_node));
  nand nand_1 (nand_1_out, R0_WE, R1_WE, R2_WE, R3_WE, R4_WE, R5_WE, R6_WE, R7_WE);
  not not_1 (not_1_out, R0_WE);
  not not_2 (not_2_out, R4_WE);
  nand nand_2 (nand_2_out, R0_OE, R1_OE, R2_OE, R3_OE, R4_OE, R5_OE, R6_OE, R7_OE);
  Register_8_Bits R0 (
    .Writes_to_register_if_0(R0_WE), .Reads_from_register_if_0(R0_OE),
    .Clock__Store_data_on_rising_edge(Clock), .Content_View__Debug(R0_Content), .Input(R0_output),
    .Output(R0_output), .Clears_the_register_when_0(pull_resistor_1_node));
  Pull_Resistor #(.pull(1)) pull_resistor_3 (.node(pull_resistor_3_node));
  not not_3 (not_3_out, R0_OE);
  assign R0_output = not_1_out ? controlled_buffer_1_out : 8'bz;  // Controlled_Buffer controlled_buffer_3
  assign controlled_buffer_1_out = not_3_out ? R0_output : 8'bz;  // Controlled_Buffer controlled_buffer_4
  Register_8_Bits R4 (
    .Writes_to_register_if_0(R4_WE), .Reads_from_register_if_0(R4_OE),
    .Clock__Store_data_on_rising_edge(Clock), .Content_View__Debug(R4_Content), .Input(R4_output),
    .Output(R4_output), .Clears_the_register_when_0(pull_resistor_2_node));
  Pull_Resistor #(.pull(1)) pull_resistor_4 (.node(pull_resistor_4_node));
  not not_4 (not_4_out, R4_OE);
  assign R4_output = not_2_out ? controlled_buffer_1_out : 8'bz;  // Controlled_Buffer controlled_buffer_5
  assign controlled_buffer_1_out = not_4_out ? R4_output : 8'bz;  // Controlled_Buffer controlled_buffer_6
  Register_8_Bits R1 (
    .Writes_to_register_if_0(R1_WE), .Reads_from_register_if_0(R1_OE),
    .Clock__Store_data_on_rising_edge(Clock), .Content_View__Debug(R1_Content), .Input(R1_output),
    .Output(R1_output), .Clears_the_register_when_0(pull_resistor_3_node));
  not not_5 (not_5_out, R1_OE);
  not not_6 (not_6_out, R1_WE);
  assign R1_output = not_6_out ? controlled_buffer_1_out : 8'bz;  // Controlled_Buffer controlled_buffer_7
  Register_8_Bits R5 (
    .Writes_to_register_if_0(R5_WE), .Reads_from_register_if_0(R5_OE),
    .Clock__Store_data_on_rising_edge(Clock), .Content_View__Debug(R5_Content), .Input(R5_output),
    .Output(R5_output), .Clears_the_register_when_0(pull_resistor_4_node));
  not not_7 (not_7_out, R5_OE);
  not not_8 (not_8_out, R5_WE);
  assign R5_output = not_8_out ? controlled_buffer_1_out : 8'bz;  // Controlled_Buffer controlled_buffer_8
  Pull_Resistor #(.pull(1)) pull_resistor_5 (.node(pull_resistor_5_node));
  assign controlled_buffer_1_out = not_5_out ? R1_output : 8'bz;  // Controlled_Buffer controlled_buffer_9
  Pull_Resistor #(.pull(1)) pull_resistor_6 (.node(pull_resistor_6_node));
  assign controlled_buffer_1_out = not_7_out ? R5_output : 8'bz;  // Controlled_Buffer controlled_buffer_10
  not not_9 (not_9_out, R2_WE);
  not not_10 (not_10_out, R6_WE);
  Register_8_Bits R2 (
    .Writes_to_register_if_0(R2_WE), .Reads_from_register_if_0(R2_OE),
    .Clock__Store_data_on_rising_edge(Clock), .Content_View__Debug(R2_Content), .Input(R2_output),
    .Output(R2_output), .Clears_the_register_when_0(pull_resistor_5_node));
  Pull_Resistor #(.pull(1)) pull_resistor_7 (.node(pull_resistor_7_node));
  not not_11 (not_11_out, R2_OE);
  assign controlled_buffer_1_out = not_11_out ? R2_output : 8'bz;  // Controlled_Buffer controlled_buffer_11
  assign R2_output = not_9_out ? controlled_buffer_1_out : 8'bz;  // Controlled_Buffer controlled_buffer_12
  Register_8_Bits R6 (
    .Writes_to_register_if_0(R6_WE), .Reads_from_register_if_0(R6_OE),
    .Clock__Store_data_on_rising_edge(Clock), .Content_View__Debug(R6_Content), .Input(R6_output),
    .Output(R6_output), .Clears_the_register_when_0(pull_resistor_6_node));
  Pull_Resistor #(.pull(1)) pull_resistor_8 (.node(pull_resistor_8_node));
  not not_12 (not_12_out, R6_OE);
  assign controlled_buffer_1_out = not_12_out ? R6_output : 8'bz;  // Controlled_Buffer controlled_buffer_13
  assign R6_output = not_10_out ? controlled_buffer_1_out : 8'bz;  // Controlled_Buffer controlled_buffer_14
  Register_8_Bits R3 (
    .Writes_to_register_if_0(R3_WE), .Reads_from_register_if_0(R3_OE),
    .Clock__Store_data_on_rising_edge(Clock), .Content_View__Debug(R3_Content), .Input(R3_output),
    .Output(R3_output), .Clears_the_register_when_0(pull_resistor_7_node));
  not not_13 (not_13_out, R3_OE);
  not not_14 (not_14_out, R3_WE);
  assign R3_output = not_14_out ? controlled_buffer_1_out : 8'bz;  // Controlled_Buffer controlled_buffer_15
  Register_8_Bits R7 (
    .Writes_to_register_if_0(R7_WE), .Reads_from_register_if_0(R7_OE),
    .Clock__Store_data_on_rising_edge(Clock), .Content_View__Debug(R7_Content), .Input(R7_output),
    .Output(R7_output), .Clears_the_register_when_0(pull_resistor_8_node));
  not not_15 (not_15_out, R7_OE);
  not not_16 (not_16_out, R7_WE);
  assign R7_output = not_16_out ? controlled_buffer_1_out : 8'bz;  // Controlled_Buffer controlled_buffer_16
  assign controlled_buffer_1_out = not_13_out ? R3_output : 8'bz;  // Controlled_Buffer controlled_buffer_17
  assign controlled_buffer_1_out = not_15_out ? R7_output : 8'bz;  // Controlled_Buffer controlled_buffer_18

  // Notes on the sheet:
  //   Bus I/O 3-State Emulation
endmodule

// AREGS
module Address_Registers (
  input  ADDR0H_WE,
  input  ADDR0H_OE,
  input  ADDR0L_WE,
  input  ADDR0L_OE,
  input  ADDR1H_WE,
  input  ADDR1H_OE,
  input  ADDR1L_WE,
  input  ADDR1L_OE,
  input  IPH_WE,
  input  IPH_OE,
  input  IPL_WE,
  input  IPL_OE,
  input  [7:0] Register_Data_Bus,
  input  Clock,
  output [7:0] Register_Data_Bus_2,
  output [7:0] ADDR0H_Content,
  output [7:0] ADDR0L_Content,
  output [7:0] ADDR1H_Content,
  output [7:0] ADDR1L_Content,
  output [7:0] IPH_Content,
  output [7:0] IPL_Content
);

  wire and_1_out, nand_1_out, nand_2_out, not_1_out, not_2_out, not_3_out, not_4_out, not_5_out, not_6_out,
       not_7_out, not_8_out, not_9_out, not_10_out, not_11_out, not_12_out, pull_resistor_1_node,
       pull_resistor_2_node, pull_resistor_3_node, pull_resistor_4_node, pull_resistor_5_node,
       pull_resistor_6_node;
  wire [7:0] ADDR0H_output, ADDR0L_output, ADDR1H_output, ADDR1L_output, controlled_buffer_1_out, IPH_output,
       IPL_output;

  and and_1 (and_1_out, ~nand_2_out, nand_1_out);  // AND_Gate
  assign controlled_buffer_1_out = and_1_out ? Register_Data_Bus : 8'bz;  // Controlled_Buffer controlled_buffer_1
  assign Register_Data_Bus_2 = nand_2_out ? controlled_buffer_1_out : 8'bz;  // Controlled_Buffer controlled_buffer_2
  Pull_Resistor #(.pull(1)) pull_resistor_1 (.node(pull_resistor_1_node));
  Pull_Resistor #(.pull(1)) pull_resistor_2 (.node(pull_resistor_2_node));
  nand nand_1 (nand_1_out, ADDR0H_WE, ADDR0L_WE, ADDR1H_WE, ADDR1L_WE, IPH_WE, IPL_WE);
  not not_1 (not_1_out, ADDR0H_WE);
  not not_2 (not_2_out, IPH_WE);
  nand nand_2 (nand_2_out, ADDR0H_OE, ADDR0L_OE, ADDR1H_OE, ADDR1L_OE, IPH_OE, IPL_OE);
  Register_8_Bits ADDR0H (
    .Writes_to_register_if_0(ADDR0H_WE), .Reads_from_register_if_0(ADDR0H_OE),
    .Clock__Store_data_on_rising_edge(Clock), .Content_View__Debug(ADDR0H_Content), .Input(ADDR0H_output),
    .Output(ADDR0H_output), .Clears_the_register_when_0(pull_resistor_1_node));
  Pull_Resistor #(.pull(1)) pull_resistor_3 (.node(pull_resistor_3_node));
  not not_3 (not_3_out, ADDR0H_OE);
  assign ADDR0H_output = not_1_out ? controlled_buffer_1_out : 8'bz;  // Controlled_Buffer controlled_buffer_3
  assign controlled_buffer_1_out = not_3_out ? ADDR0H_output : 8'bz;  // Controlled_Buffer controlled_buffer_4
  Register_8_Bits IPH (
    .Writes_to_register_if_0(IPH_WE), .Reads_from_register_if_0(IPH_OE),
    .Clock__Store_data_on_rising_edge(Clock), .Content_View__Debug(IPH_Content), .Input(IPH_output),
    .Output(IPH_output), .Clears_the_register_when_0(pull_resistor_2_node));
  Pull_Resistor #(.pull(1)) pull_resistor_4 (.node(pull_resistor_4_node));
  not not_4 (not_4_out, IPH_OE);
  assign IPH_output = not_2_out ? controlled_buffer_1_out : 8'bz;  // Controlled_Buffer controlled_buffer_5
  assign controlled_buffer_1_out = not_4_out ? IPH_output : 8'bz;  // Controlled_Buffer controlled_buffer_6
  Register_8_Bits ADDR0L (
    .Writes_to_register_if_0(ADDR0L_WE), .Reads_from_register_if_0(ADDR0L_OE),
    .Clock__Store_data_on_rising_edge(Clock), .Content_View__Debug(ADDR0L_Content), .Input(ADDR0L_output),
    .Output(ADDR0L_output), .Clears_the_register_when_0(pull_resistor_3_node));
  not not_5 (not_5_out, ADDR0L_OE);
  not not_6 (not_6_out, ADDR0L_WE);
  assign ADDR0L_output = not_6_out ? controlled_buffer_1_out : 8'bz;  // Controlled_Buffer controlled_buffer_7
  Register_8_Bits IPL (
    .Writes_to_register_if_0(IPL_WE), .Reads_from_register_if_0(IPL_OE),
    .Clock__Store_data_on_rising_edge(Clock), .Content_View__Debug(IPL_Content), .Input(IPL_output),
    .Output(IPL_output), .Clears_the_register_when_0(pull_resistor_4_node));
  not not_7 (not_7_out, IPL_OE);
  not not_8 (not_8_out, IPL_WE);
  assign IPL_output = not_8_out ? controlled_buffer_1_out : 8'bz;  // Controlled_Buffer controlled_buffer_8
  Pull_Resistor #(.pull(1)) pull_resistor_5 (.node(pull_resistor_5_node));
  assign controlled_buffer_1_out = not_5_out ? ADDR0L_output : 8'bz;  // Controlled_Buffer controlled_buffer_9
  assign controlled_buffer_1_out = not_7_out ? IPL_output : 8'bz;  // Controlled_Buffer controlled_buffer_10
  not not_9 (not_9_out, ADDR1H_WE);
  Register_8_Bits ADDR1H (
    .Writes_to_register_if_0(ADDR1H_WE), .Reads_from_register_if_0(ADDR1H_OE),
    .Clock__Store_data_on_rising_edge(Clock), .Content_View__Debug(ADDR1H_Content), .Input(ADDR1H_output),
    .Output(ADDR1H_output), .Clears_the_register_when_0(pull_resistor_5_node));
  Pull_Resistor #(.pull(1)) pull_resistor_6 (.node(pull_resistor_6_node));
  not not_10 (not_10_out, ADDR1H_OE);
  assign ADDR1H_output = not_9_out ? controlled_buffer_1_out : 8'bz;  // Controlled_Buffer controlled_buffer_11
  assign controlled_buffer_1_out = not_10_out ? ADDR1H_output : 8'bz;  // Controlled_Buffer controlled_buffer_12
  Register_8_Bits ADDR1L (
    .Writes_to_register_if_0(ADDR1L_WE), .Reads_from_register_if_0(ADDR1L_OE),
    .Clock__Store_data_on_rising_edge(Clock), .Content_View__Debug(ADDR1L_Content), .Input(ADDR1L_output),
    .Output(ADDR1L_output), .Clears_the_register_when_0(pull_resistor_6_node));
  not not_11 (not_11_out, ADDR1L_OE);
  not not_12 (not_12_out, ADDR1L_WE);
  assign ADDR1L_output = not_12_out ? controlled_buffer_1_out : 8'bz;  // Controlled_Buffer controlled_buffer_13
  assign controlled_buffer_1_out = not_11_out ? ADDR1L_output : 8'bz;  // Controlled_Buffer controlled_buffer_14

  // Notes on the sheet:
  //   Bus I/O 3-State Emulation
endmodule

// SREGS
module Special_Registers (
  input  SP_WE,
  input  SP_OE,
  input  SR_WE,
  input  SR_OE,
  input  [7:0] Register_Data_Bus,
  input  MR_WE,
  input  MR_OE,
  input  [7:0] Masking_Bus,
  input  Clock,
  output [7:0] Register_Data_Bus_2,
  output [7:0] SP_Content,
  output [7:0] SB_Content,
  output [7:0] MR_Content
);

  wire and_1_out, nand_1_out, nand_2_out, not_1_out, not_2_out, not_3_out, not_4_out, not_5_out, not_6_out,
       pull_resistor_1_node, pull_resistor_2_node, pull_resistor_3_node;
  wire [7:0] controlled_buffer_1_out, MR_output, SB_dout, SP_output;

  and and_1 (and_1_out, ~nand_2_out, nand_1_out);  // AND_Gate
  assign controlled_buffer_1_out = and_1_out ? Register_Data_Bus : 8'bz;  // Controlled_Buffer controlled_buffer_1
  assign Register_Data_Bus_2 = nand_2_out ? controlled_buffer_1_out : 8'bz;  // Controlled_Buffer controlled_buffer_2
  Pull_Resistor #(.pull(1)) pull_resistor_1 (.node(pull_resistor_1_node));
  nand nand_1 (nand_1_out, SP_WE, SR_WE, MR_WE);
  not not_1 (not_1_out, SP_WE);
  nand nand_2 (nand_2_out, SP_OE, SR_OE, MR_OE);
  Register_8_Bits SP (
    .Writes_to_register_if_0(SP_WE), .Reads_from_register_if_0(SP_OE),
    .Clock__Store_data_on_rising_edge(Clock), .Content_View__Debug(SP_Content), .Input(SP_output),
    .Output(SP_output), .Clears_the_register_when_0(pull_resistor_1_node));
  Pull_Resistor #(.pull(1)) pull_resistor_2 (.node(pull_resistor_2_node));
  not not_2 (not_2_out, SP_OE);
  assign controlled_buffer_1_out = not_2_out ? SP_output : 8'bz;  // Controlled_Buffer controlled_buffer_3
  assign SP_output = not_1_out ? controlled_buffer_1_out : 8'bz;  // Controlled_Buffer controlled_buffer_4
  Maskable_Register_8_bits SB (
    .Writes_to_register_if_0(SR_WE), .Reads_from_register_if_0(SR_OE),
    .Clock__Store_data_on_rising_edge(Clock), .Clears_the_register_when_0(pull_resistor_2_node),
    .Content_View__Debug(SB_Content), .DIn(SB_dout), .DOut(SB_dout), .Bitmask(Masking_Bus));
  not not_3 (not_3_out, SR_OE);
  not not_4 (not_4_out, SR_WE);
  assign SB_dout = not_4_out ? controlled_buffer_1_out : 8'bz;  // Controlled_Buffer controlled_buffer_5
  Pull_Resistor #(.pull(1)) pull_resistor_3 (.node(pull_resistor_3_node));
  assign controlled_buffer_1_out = not_3_out ? SB_dout : 8'bz;  // Controlled_Buffer controlled_buffer_6
  not not_5 (not_5_out, MR_WE);
  Register_8_Bits MR (
    .Writes_to_register_if_0(MR_WE), .Reads_from_register_if_0(MR_OE),
    .Clock__Store_data_on_rising_edge(Clock), .Content_View__Debug(MR_Content), .Input(MR_output),
    .Output(MR_output), .Clears_the_register_when_0(pull_resistor_3_node));
  not not_6 (not_6_out, MR_OE);
  assign controlled_buffer_1_out = not_6_out ? MR_output : 8'bz;  // Controlled_Buffer controlled_buffer_7
  assign MR_output = not_5_out ? controlled_buffer_1_out : 8'bz;  // Controlled_Buffer controlled_buffer_8

  // Notes on the sheet:
  //   Bus I/O 3-State Emulation
endmodule

// TICK
module Tick_Register (
  input  Byte_Select_0,
  input  Byte_Select_1,
  input  Byte_Select_2,
  input  Read,
  input  Falling_edge_triggered_clock,
  output [7:0] out_6,
  output [7:0] Byte_0,
  output [7:0] Byte_1,
  output [7:0] Byte_2,
  output [7:0] Byte_3,
  output [7:0] Byte_4,
  output [7:0] Byte_5,
  output [7:0] Byte_6
);

  wire and_1_out, and_2_out, and_3_out, and_4_out, and_5_out, and_6_out, and_7_out, and_8_out, and_9_out,
       and_10_out, and_11_out, and_12_out, and_13_out, and_14_out, and_15_out,
       n74138_3_to_8_line_decoder_1_out_7, n74138_3_to_8_line_decoder_1_out_8,
       n74138_3_to_8_line_decoder_1_out_9, n74138_3_to_8_line_decoder_1_out_10,
       n74138_3_to_8_line_decoder_1_out_11, n74138_3_to_8_line_decoder_1_out_12,
       n74138_3_to_8_line_decoder_1_out_13, not_1_out, not_2_out, not_3_out, not_4_out, not_5_out, not_6_out,
       not_7_out, not_8_out;

  and and_1 (and_1_out, Byte_0[0], Byte_0[1], Byte_0[2], Byte_0[3]);
  and and_2 (and_2_out, Byte_0[4], Byte_0[5], Byte_0[6], Byte_0[7]);
  and and_3 (and_3_out, Byte_1[0], Byte_1[1], Byte_1[2]);
  and and_4 (and_4_out, Byte_1[3], Byte_1[4], Byte_1[5]);
  and and_5 (and_5_out, Byte_1[6], Byte_1[7], Byte_2[0], Byte_2[1]);
  and and_6 (and_6_out, Byte_2[2], Byte_2[3], Byte_2[4], Byte_2[5]);
  and and_7 (and_7_out, Byte_2[6], Byte_2[7], Byte_3[0]);
  and and_8 (and_8_out, Byte_3[1], Byte_3[2], Byte_3[3]);
  and and_9 (and_9_out, Byte_3[4], Byte_3[5], Byte_3[6], Byte_3[7]);
  and and_10 (and_10_out, Byte_4[0], Byte_4[1], Byte_4[2], Byte_4[3]);
  and and_11 (and_11_out, Byte_4[4], Byte_4[5], Byte_4[6]);
  and and_12 (and_12_out, Byte_4[7], Byte_5[0], Byte_5[1]);
  not not_1 (not_1_out, Read);
  _74138_3_to_8_Line_Decoder u_74138_3_to_8_line_decoder_1 (
    .Enabled_when_0_2(not_1_out), .Data_Select_0(Byte_Select_0), .Data_Select_1(Byte_Select_1),
    .Data_Select_2(Byte_Select_2), .out_7(n74138_3_to_8_line_decoder_1_out_7),
    .out_8(n74138_3_to_8_line_decoder_1_out_8), .out_9(n74138_3_to_8_line_decoder_1_out_9),
    .out_10(n74138_3_to_8_line_decoder_1_out_10), .out_11(n74138_3_to_8_line_decoder_1_out_11),
    .out_12(n74138_3_to_8_line_decoder_1_out_12), .out_13(n74138_3_to_8_line_decoder_1_out_13),
    .Enabled_when_0(not_1_out), .Enabled_when_1(Read));  // open: out_14
  and and_13 (and_13_out, and_1_out, and_2_out, and_3_out, and_4_out);
  and and_14 (and_14_out, and_5_out, and_6_out, and_7_out, and_8_out);
  and and_15 (and_15_out, and_9_out, and_10_out, and_11_out, and_12_out);
  _744020_14_Stage_Binary_Counter _744020 (
    .Clock__Count_on_falling_edge(Falling_edge_triggered_clock), .Master_Reset(1'b0), .out_3(Byte_0[0]),
    .out_4(Byte_0[1]), .out_5(Byte_0[2]), .out_6(Byte_0[3]), .out_7(Byte_0[4]), .out_8(Byte_0[5]),
    .out_9(Byte_0[6]), .out_10(Byte_0[7]), .out_11(Byte_1[0]), .out_12(Byte_1[1]), .out_13(Byte_1[2]),
    .out_14(Byte_1[3]), .out_15(Byte_1[4]), .out_16(Byte_1[5]));
  _744020_14_Stage_Binary_Counter _744020_2 (
    .Clock__Count_on_falling_edge(and_13_out), .Master_Reset(1'b0), .out_3(Byte_1[6]), .out_4(Byte_1[7]),
    .out_5(Byte_2[0]), .out_6(Byte_2[1]), .out_7(Byte_2[2]), .out_8(Byte_2[3]), .out_9(Byte_2[4]),
    .out_10(Byte_2[5]), .out_11(Byte_2[6]), .out_12(Byte_2[7]), .out_13(Byte_3[0]), .out_14(Byte_3[1]),
    .out_15(Byte_3[2]), .out_16(Byte_3[3]));
  _744020_14_Stage_Binary_Counter _744020_3 (
    .Clock__Count_on_falling_edge(and_14_out), .Master_Reset(1'b0), .out_3(Byte_3[4]), .out_4(Byte_3[5]),
    .out_5(Byte_3[6]), .out_6(Byte_3[7]), .out_7(Byte_4[0]), .out_8(Byte_4[1]), .out_9(Byte_4[2]),
    .out_10(Byte_4[3]), .out_11(Byte_4[4]), .out_12(Byte_4[5]), .out_13(Byte_4[6]), .out_14(Byte_4[7]),
    .out_15(Byte_5[0]), .out_16(Byte_5[1]));
  _744020_14_Stage_Binary_Counter _744020_4 (
    .Clock__Count_on_falling_edge(and_15_out), .Master_Reset(1'b0), .out_3(Byte_5[2]), .out_4(Byte_5[3]),
    .out_5(Byte_5[4]), .out_6(Byte_5[5]), .out_7(Byte_5[6]), .out_8(Byte_5[7]), .out_9(Byte_6[0]),
    .out_10(Byte_6[1]), .out_11(Byte_6[2]), .out_12(Byte_6[3]), .out_13(Byte_6[4]), .out_14(Byte_6[5]),
    .out_15(Byte_6[6]), .out_16(Byte_6[7]));
  not not_2 (not_2_out, n74138_3_to_8_line_decoder_1_out_7);
  not not_3 (not_3_out, n74138_3_to_8_line_decoder_1_out_8);
  not not_4 (not_4_out, n74138_3_to_8_line_decoder_1_out_9);
  not not_5 (not_5_out, n74138_3_to_8_line_decoder_1_out_10);
  not not_6 (not_6_out, n74138_3_to_8_line_decoder_1_out_11);
  not not_7 (not_7_out, n74138_3_to_8_line_decoder_1_out_12);
  not not_8 (not_8_out, n74138_3_to_8_line_decoder_1_out_13);
  _74373_Octal_D_Latch_3S _74373 (
    ._1D(Byte_0[0]), ._2D(Byte_0[1]), ._3D(Byte_0[2]), ._4D(Byte_0[3]), ._5D(Byte_0[4]), ._6D(Byte_0[5]),
    ._7D(Byte_0[6]), ._8D(Byte_0[7]), .Load_data_when_1(not_2_out),
    .Output_enabled_when_0(n74138_3_to_8_line_decoder_1_out_7), ._1Q(out_6[0]), ._2Q(out_6[1]),
    ._3Q(out_6[2]), ._4Q(out_6[3]), ._5Q(out_6[4]), ._6Q(out_6[5]), ._7Q(out_6[6]), ._8Q(out_6[7]));
  _74373_Octal_D_Latch_3S _74373_2 (
    ._1D(Byte_1[0]), ._2D(Byte_1[1]), ._3D(Byte_1[2]), ._4D(Byte_1[3]), ._5D(Byte_1[4]), ._6D(Byte_1[5]),
    ._7D(Byte_1[6]), ._8D(Byte_1[7]), .Load_data_when_1(not_3_out),
    .Output_enabled_when_0(n74138_3_to_8_line_decoder_1_out_8), ._1Q(out_6[0]), ._2Q(out_6[1]),
    ._3Q(out_6[2]), ._4Q(out_6[3]), ._5Q(out_6[4]), ._6Q(out_6[5]), ._7Q(out_6[6]), ._8Q(out_6[7]));
  _74373_Octal_D_Latch_3S _74373_3 (
    ._1D(Byte_2[0]), ._2D(Byte_2[1]), ._3D(Byte_2[2]), ._4D(Byte_2[3]), ._5D(Byte_2[4]), ._6D(Byte_2[5]),
    ._7D(Byte_2[6]), ._8D(Byte_2[7]), .Load_data_when_1(not_4_out),
    .Output_enabled_when_0(n74138_3_to_8_line_decoder_1_out_9), ._1Q(out_6[0]), ._2Q(out_6[1]),
    ._3Q(out_6[2]), ._4Q(out_6[3]), ._5Q(out_6[4]), ._6Q(out_6[5]), ._7Q(out_6[6]), ._8Q(out_6[7]));
  _74373_Octal_D_Latch_3S _74373_4 (
    ._1D(Byte_3[0]), ._2D(Byte_3[1]), ._3D(Byte_3[2]), ._4D(Byte_3[3]), ._5D(Byte_3[4]), ._6D(Byte_3[5]),
    ._7D(Byte_3[6]), ._8D(Byte_3[7]), .Load_data_when_1(not_5_out),
    .Output_enabled_when_0(n74138_3_to_8_line_decoder_1_out_10), ._1Q(out_6[0]), ._2Q(out_6[1]),
    ._3Q(out_6[2]), ._4Q(out_6[3]), ._5Q(out_6[4]), ._6Q(out_6[5]), ._7Q(out_6[6]), ._8Q(out_6[7]));
  _74373_Octal_D_Latch_3S _74373_5 (
    ._1D(Byte_4[0]), ._2D(Byte_4[1]), ._3D(Byte_4[2]), ._4D(Byte_4[3]), ._5D(Byte_4[4]), ._6D(Byte_4[5]),
    ._7D(Byte_4[6]), ._8D(Byte_4[7]), .Load_data_when_1(not_6_out),
    .Output_enabled_when_0(n74138_3_to_8_line_decoder_1_out_11), ._1Q(out_6[0]), ._2Q(out_6[1]),
    ._3Q(out_6[2]), ._4Q(out_6[3]), ._5Q(out_6[4]), ._6Q(out_6[5]), ._7Q(out_6[6]), ._8Q(out_6[7]));
  _74373_Octal_D_Latch_3S _74373_6 (
    ._1D(Byte_5[0]), ._2D(Byte_5[1]), ._3D(Byte_5[2]), ._4D(Byte_5[3]), ._5D(Byte_5[4]), ._6D(Byte_5[5]),
    ._7D(Byte_5[6]), ._8D(Byte_5[7]), .Load_data_when_1(not_7_out),
    .Output_enabled_when_0(n74138_3_to_8_line_decoder_1_out_12), ._1Q(out_6[0]), ._2Q(out_6[1]),
    ._3Q(out_6[2]), ._4Q(out_6[3]), ._5Q(out_6[4]), ._6Q(out_6[5]), ._7Q(out_6[6]), ._8Q(out_6[7]));
  _74373_Octal_D_Latch_3S _74373_7 (
    ._1D(Byte_6[0]), ._2D(Byte_6[1]), ._3D(Byte_6[2]), ._4D(Byte_6[3]), ._5D(Byte_6[4]), ._6D(Byte_6[5]),
    ._7D(Byte_6[6]), ._8D(Byte_6[7]), .Load_data_when_1(not_8_out),
    .Output_enabled_when_0(n74138_3_to_8_line_decoder_1_out_13), ._1Q(out_6[0]), ._2Q(out_6[1]),
    ._3Q(out_6[2]), ._4Q(out_6[3]), ._5Q(out_6[4]), ._6Q(out_6[5]), ._7Q(out_6[6]), ._8Q(out_6[7]));

  // Other names for the same wires on the sheet: D0 = Byte_0[0]; D1 = Byte_0[1]; D2 = Byte_0[2]; D3 = Byte_0[3];
  //   D4 = Byte_0[4]; D5 = Byte_0[5]; D6 = Byte_0[6]; D7 = Byte_0[7]; D8 = Byte_1[0]; D9 = Byte_1[1]; D10 = Byte_1[2];
  //   D11 = Byte_1[3]; D12 = Byte_1[4]; D13 = Byte_1[5]; D14 = Byte_1[6]; D15 = Byte_1[7]; D16 = Byte_2[0];
  //   D17 = Byte_2[1]; D18 = Byte_2[2]; D19 = Byte_2[3]; D20 = Byte_2[4]; D21 = Byte_2[5]; D22 = Byte_2[6];
  //   D23 = Byte_2[7]; D24 = Byte_3[0]; D25 = Byte_3[1]; D26 = Byte_3[2]; D27 = Byte_3[3]; D28 = Byte_3[4];
  //   D29 = Byte_3[5]; D30 = Byte_3[6]; D31 = Byte_3[7]; D32 = Byte_4[0]; D33 = Byte_4[1]; D34 = Byte_4[2];
  //   D35 = Byte_4[3]; D36 = Byte_4[4]; D37 = Byte_4[5]; D38 = Byte_4[6]; D39 = Byte_4[7]; D40 = Byte_5[0];
  //   D41 = Byte_5[1]; D42 = Byte_5[2]; D43 = Byte_5[3]; D44 = Byte_5[4]; D45 = Byte_5[5]; D46 = Byte_5[6];
  //   D47 = Byte_5[7]; D48 = Byte_6[0]; D49 = Byte_6[1]; D50 = Byte_6[2]; D51 = Byte_6[3]; D52 = Byte_6[4];
  //   D53 = Byte_6[5]; D54 = Byte_6[6]; D55 = Byte_6[7]
endmodule

module Register_16_Bits (
  input  Writes_to_register_if_0,
  input  Reads_from_register_if_low,
  input  Clock__Stores_data_on_rising_edgeEdge,
  input  Clears_the_register_when_0,
  input  [15:0] Data_Input,
  output [15:0] Content_View__Debug,
  output [15:0] Data_output
);

  wire _7432_out, _7486_out, _74245_2_out_19, _74245_2_out_21, _74245_2_out_23, _74245_2_out_25,
       _74245_2_out_27, _74245_2_out_29, _74245_2_out_31, _74245_2_out_33, _74245_out_19, _74245_out_21,
       _74245_out_23, _74245_out_25, _74245_out_27, _74245_out_29, _74245_out_31, _74245_out_33, not_1_out,
       not_2_out, not_3_out, not_4_out;
  wire [15:0] controlled_buffer_1_out;

  not not_1 (not_1_out, Writes_to_register_if_0);
  assign controlled_buffer_1_out = not_1_out ? Data_Input : 16'bz;  // Controlled_Buffer controlled_buffer_1
  not not_2 (not_2_out, Reads_from_register_if_low);
  assign Data_output = not_2_out ? controlled_buffer_1_out : 16'bz;  // Controlled_Buffer controlled_buffer_2
  xor _7486 (_7486_out, Reads_from_register_if_low, Writes_to_register_if_0);
  not not_3 (not_3_out, Writes_to_register_if_0);
  or _7432 (_7432_out, not_3_out, Reads_from_register_if_low);
  not not_4 (not_4_out, _7486_out);
  _74245_Octal_Bus_Transceiver_3S _74245 (
    .A0(controlled_buffer_1_out[0]), .out_20(controlled_buffer_1_out[0]), .A1(controlled_buffer_1_out[1]),
    .out_22(controlled_buffer_1_out[1]), .A2(controlled_buffer_1_out[2]),
    .out_24(controlled_buffer_1_out[2]), .A3(controlled_buffer_1_out[3]),
    .out_26(controlled_buffer_1_out[3]), .A4(controlled_buffer_1_out[4]),
    .out_28(controlled_buffer_1_out[4]), .A5(controlled_buffer_1_out[5]),
    .out_30(controlled_buffer_1_out[5]), .A6(controlled_buffer_1_out[6]),
    .out_32(controlled_buffer_1_out[6]), .A7(controlled_buffer_1_out[7]),
    .out_34(controlled_buffer_1_out[7]), .DIR(_7432_out), .out_19(_74245_out_19),
    .B0(Content_View__Debug[0]), .out_21(_74245_out_21), .B1(Content_View__Debug[1]), .out_23(_74245_out_23),
    .B2(Content_View__Debug[2]), .out_25(_74245_out_25), .B3(Content_View__Debug[3]), .out_27(_74245_out_27),
    .B4(Content_View__Debug[4]), .out_29(_74245_out_29), .B5(Content_View__Debug[5]), .out_31(_74245_out_31),
    .B6(Content_View__Debug[6]), .out_33(_74245_out_33), .B7(Content_View__Debug[7]), .OE(not_4_out));
  _74245_Octal_Bus_Transceiver_3S _74245_2 (
    .A0(controlled_buffer_1_out[8]), .out_20(controlled_buffer_1_out[8]), .A1(controlled_buffer_1_out[9]),
    .out_22(controlled_buffer_1_out[9]), .A2(controlled_buffer_1_out[10]),
    .out_24(controlled_buffer_1_out[10]), .A3(controlled_buffer_1_out[11]),
    .out_26(controlled_buffer_1_out[11]), .A4(controlled_buffer_1_out[12]),
    .out_28(controlled_buffer_1_out[12]), .A5(controlled_buffer_1_out[13]),
    .out_30(controlled_buffer_1_out[13]), .A6(controlled_buffer_1_out[14]),
    .out_32(controlled_buffer_1_out[14]), .A7(controlled_buffer_1_out[15]),
    .out_34(controlled_buffer_1_out[15]), .DIR(_7432_out), .out_19(_74245_2_out_19),
    .B0(Content_View__Debug[8]), .out_21(_74245_2_out_21), .B1(Content_View__Debug[9]),
    .out_23(_74245_2_out_23), .B2(Content_View__Debug[10]), .out_25(_74245_2_out_25),
    .B3(Content_View__Debug[11]), .out_27(_74245_2_out_27), .B4(Content_View__Debug[12]),
    .out_29(_74245_2_out_29), .B5(Content_View__Debug[13]), .out_31(_74245_2_out_31),
    .B6(Content_View__Debug[14]), .out_33(_74245_2_out_33), .B7(Content_View__Debug[15]), .OE(not_4_out));
  _74273_Octal_D_Flip_Flip _74273 (
    .CP(Clock__Stores_data_on_rising_edgeEdge), .D0(_74245_out_19), .D1(_74245_out_21), .D2(_74245_out_23),
    .D3(_74245_out_25), .D4(_74245_out_27), .D5(_74245_out_29), .D6(_74245_out_31), .D7(_74245_out_33),
    .MR(Clears_the_register_when_0), .Q0(Content_View__Debug[0]), .Q1(Content_View__Debug[1]),
    .Q2(Content_View__Debug[2]), .Q3(Content_View__Debug[3]), .Q4(Content_View__Debug[4]),
    .Q5(Content_View__Debug[5]), .Q6(Content_View__Debug[6]), .Q7(Content_View__Debug[7]));
  _74273_Octal_D_Flip_Flip _74273_2 (
    .CP(Clock__Stores_data_on_rising_edgeEdge), .D0(_74245_2_out_19), .D1(_74245_2_out_21),
    .D2(_74245_2_out_23), .D3(_74245_2_out_25), .D4(_74245_2_out_27), .D5(_74245_2_out_29),
    .D6(_74245_2_out_31), .D7(_74245_2_out_33), .MR(Clears_the_register_when_0), .Q0(Content_View__Debug[8]),
    .Q1(Content_View__Debug[9]), .Q2(Content_View__Debug[10]), .Q3(Content_View__Debug[11]),
    .Q4(Content_View__Debug[12]), .Q5(Content_View__Debug[13]), .Q6(Content_View__Debug[14]),
    .Q7(Content_View__Debug[15]));

  // Notes on the sheet:
  //   Bus I/O 3-State Emulation
endmodule

module Register_8_Bits (
  input  Writes_to_register_if_0,
  input  Reads_from_register_if_0,
  input  Clock__Store_data_on_rising_edge,
  input  Clears_the_register_when_0,
  input  [7:0] Input,
  output [7:0] Content_View__Debug,
  output [7:0] Output
);

  wire _7432_out, _7486_out, _74245_out_19, _74245_out_21, _74245_out_23, _74245_out_25, _74245_out_27,
       _74245_out_29, _74245_out_31, _74245_out_33, not_1_out, not_2_out, not_3_out, not_4_out;
  wire [7:0] controlled_buffer_2_out;

  not not_1 (not_1_out, Writes_to_register_if_0);
  not not_2 (not_2_out, Writes_to_register_if_0);
  not not_3 (not_3_out, Reads_from_register_if_0);
  assign Output = not_3_out ? controlled_buffer_2_out : 8'bz;  // Controlled_Buffer controlled_buffer_1
  assign controlled_buffer_2_out = not_1_out ? Input : 8'bz;  // Controlled_Buffer controlled_buffer_2
  xor _7486 (_7486_out, Reads_from_register_if_0, Writes_to_register_if_0);
  not not_4 (not_4_out, _7486_out);
  or _7432 (_7432_out, not_2_out, Reads_from_register_if_0);
  _74245_Octal_Bus_Transceiver_3S _74245 (
    .A0(controlled_buffer_2_out[0]), .out_20(controlled_buffer_2_out[0]), .A1(controlled_buffer_2_out[1]),
    .out_22(controlled_buffer_2_out[1]), .A2(controlled_buffer_2_out[2]),
    .out_24(controlled_buffer_2_out[2]), .A3(controlled_buffer_2_out[3]),
    .out_26(controlled_buffer_2_out[3]), .A4(controlled_buffer_2_out[4]),
    .out_28(controlled_buffer_2_out[4]), .A5(controlled_buffer_2_out[5]),
    .out_30(controlled_buffer_2_out[5]), .A6(controlled_buffer_2_out[6]),
    .out_32(controlled_buffer_2_out[6]), .A7(controlled_buffer_2_out[7]),
    .out_34(controlled_buffer_2_out[7]), .DIR(_7432_out), .out_19(_74245_out_19),
    .B0(Content_View__Debug[0]), .out_21(_74245_out_21), .B1(Content_View__Debug[1]), .out_23(_74245_out_23),
    .B2(Content_View__Debug[2]), .out_25(_74245_out_25), .B3(Content_View__Debug[3]), .out_27(_74245_out_27),
    .B4(Content_View__Debug[4]), .out_29(_74245_out_29), .B5(Content_View__Debug[5]), .out_31(_74245_out_31),
    .B6(Content_View__Debug[6]), .out_33(_74245_out_33), .B7(Content_View__Debug[7]), .OE(not_4_out));
  _74273_Octal_D_Flip_Flip _74273 (
    .CP(Clock__Store_data_on_rising_edge), .D0(_74245_out_19), .D1(_74245_out_21), .D2(_74245_out_23),
    .D3(_74245_out_25), .D4(_74245_out_27), .D5(_74245_out_29), .D6(_74245_out_31), .D7(_74245_out_33),
    .MR(Clears_the_register_when_0), .Q0(Content_View__Debug[0]), .Q1(Content_View__Debug[1]),
    .Q2(Content_View__Debug[2]), .Q3(Content_View__Debug[3]), .Q4(Content_View__Debug[4]),
    .Q5(Content_View__Debug[5]), .Q6(Content_View__Debug[6]), .Q7(Content_View__Debug[7]));

  // Notes on the sheet:
  //   Bus I/O 3-State Emulation
endmodule

module Maskable_Register_8_bits (
  input  Writes_to_register_if_0,
  input  Reads_from_register_if_0,
  input  Clock__Store_data_on_rising_edge,
  input  Clears_the_register_when_0,
  input  [7:0] DIn,
  input  [7:0] Bitmask,
  output [7:0] Content_View__Debug,
  output [7:0] DOut
);

  wire _7432_out, _7486_out, _74245_out_19, _74245_out_20, _74245_out_21, _74245_out_22, _74245_out_23,
       _74245_out_24, _74245_out_25, _74245_out_26, _74245_out_27, _74245_out_28, _74245_out_29,
       _74245_out_30, _74245_out_31, _74245_out_32, _74245_out_33, _74245_out_34, controlled_buffer_11_out,
       controlled_buffer_12_out, controlled_buffer_13_out, controlled_buffer_14_out,
       controlled_buffer_15_out, controlled_buffer_16_out, controlled_buffer_17_out,
       controlled_buffer_18_out, not_1_out, not_2_out, not_3_out, not_4_out, not_5_out, not_6_out, not_7_out,
       not_8_out, not_9_out, not_10_out, not_11_out, not_12_out;
  wire [7:0] controlled_buffer_1_out;

  not not_1 (not_1_out, Writes_to_register_if_0);
  assign controlled_buffer_1_out = not_1_out ? DIn : 8'bz;  // Controlled_Buffer controlled_buffer_1
  not not_2 (not_2_out, Reads_from_register_if_0);
  assign DOut = not_2_out ? controlled_buffer_1_out : 8'bz;  // Controlled_Buffer controlled_buffer_2
  xor _7486 (_7486_out, Writes_to_register_if_0, Reads_from_register_if_0);
  not not_3 (not_3_out, Writes_to_register_if_0);
  or _7432 (_7432_out, not_3_out, Reads_from_register_if_0);
  Pull_Resistor pull_resistor_1 (.node(controlled_buffer_1_out[6]));
  Pull_Resistor pull_resistor_2 (.node(controlled_buffer_1_out[2]));
  Pull_Resistor pull_resistor_3 (.node(controlled_buffer_1_out[3]));
  Pull_Resistor pull_resistor_4 (.node(controlled_buffer_1_out[5]));
  Pull_Resistor pull_resistor_5 (.node(controlled_buffer_1_out[4]));
  Pull_Resistor pull_resistor_6 (.node(controlled_buffer_1_out[7]));
  not not_4 (not_4_out, _7486_out);
  Pull_Resistor pull_resistor_7 (.node(controlled_buffer_1_out[0]));
  Pull_Resistor pull_resistor_8 (.node(controlled_buffer_1_out[1]));
  assign controlled_buffer_1_out[0] = Bitmask[0] ? _74245_out_20 : 1'bz;  // Controlled_Buffer controlled_buffer_3
  assign controlled_buffer_1_out[1] = Bitmask[1] ? _74245_out_22 : 1'bz;  // Controlled_Buffer controlled_buffer_4
  assign controlled_buffer_1_out[2] = Bitmask[2] ? _74245_out_24 : 1'bz;  // Controlled_Buffer controlled_buffer_5
  assign controlled_buffer_1_out[3] = Bitmask[3] ? _74245_out_26 : 1'bz;  // Controlled_Buffer controlled_buffer_6
  assign controlled_buffer_1_out[4] = Bitmask[4] ? _74245_out_28 : 1'bz;  // Controlled_Buffer controlled_buffer_7
  assign controlled_buffer_1_out[5] = Bitmask[5] ? _74245_out_30 : 1'bz;  // Controlled_Buffer controlled_buffer_8
  assign controlled_buffer_1_out[6] = Bitmask[6] ? _74245_out_32 : 1'bz;  // Controlled_Buffer controlled_buffer_9
  assign controlled_buffer_1_out[7] = Bitmask[7] ? _74245_out_34 : 1'bz;  // Controlled_Buffer controlled_buffer_10
  assign controlled_buffer_11_out = Bitmask[0] ? controlled_buffer_1_out[0] : 1'bz;  // Controlled_Buffer controlled_buffer_11
  assign controlled_buffer_12_out = Bitmask[1] ? controlled_buffer_1_out[1] : 1'bz;  // Controlled_Buffer controlled_buffer_12
  assign controlled_buffer_13_out = Bitmask[2] ? controlled_buffer_1_out[2] : 1'bz;  // Controlled_Buffer controlled_buffer_13
  assign controlled_buffer_14_out = Bitmask[3] ? controlled_buffer_1_out[3] : 1'bz;  // Controlled_Buffer controlled_buffer_14
  assign controlled_buffer_15_out = Bitmask[4] ? controlled_buffer_1_out[4] : 1'bz;  // Controlled_Buffer controlled_buffer_15
  assign controlled_buffer_16_out = Bitmask[5] ? controlled_buffer_1_out[5] : 1'bz;  // Controlled_Buffer controlled_buffer_16
  assign controlled_buffer_17_out = Bitmask[6] ? controlled_buffer_1_out[6] : 1'bz;  // Controlled_Buffer controlled_buffer_17
  assign controlled_buffer_18_out = Bitmask[7] ? controlled_buffer_1_out[7] : 1'bz;  // Controlled_Buffer controlled_buffer_18
  Pull_Resistor #(.pull(1)) pull_resistor_9 (.node(Bitmask[7]));
  Pull_Resistor #(.pull(1)) pull_resistor_10 (.node(Bitmask[4]));
  Pull_Resistor #(.pull(1)) pull_resistor_11 (.node(Bitmask[2]));
  Pull_Resistor #(.pull(1)) pull_resistor_12 (.node(Bitmask[5]));
  Pull_Resistor #(.pull(1)) pull_resistor_13 (.node(Bitmask[6]));
  Pull_Resistor #(.pull(1)) pull_resistor_14 (.node(Bitmask[0]));
  Pull_Resistor #(.pull(1)) pull_resistor_15 (.node(Bitmask[1]));
  Pull_Resistor #(.pull(1)) pull_resistor_16 (.node(Bitmask[3]));
  _74245_Octal_Bus_Transceiver_3S _74245 (
    .A0(controlled_buffer_11_out), .out_20(_74245_out_20), .A1(controlled_buffer_12_out),
    .out_22(_74245_out_22), .A2(controlled_buffer_13_out), .out_24(_74245_out_24),
    .A3(controlled_buffer_14_out), .out_26(_74245_out_26), .A4(controlled_buffer_15_out),
    .out_28(_74245_out_28), .A5(controlled_buffer_16_out), .out_30(_74245_out_30),
    .A6(controlled_buffer_17_out), .out_32(_74245_out_32), .A7(controlled_buffer_18_out),
    .out_34(_74245_out_34), .DIR(_7432_out), .out_19(_74245_out_19), .B0(Content_View__Debug[0]),
    .out_21(_74245_out_21), .B1(Content_View__Debug[1]), .out_23(_74245_out_23), .B2(Content_View__Debug[2]),
    .out_25(_74245_out_25), .B3(Content_View__Debug[3]), .out_27(_74245_out_27), .B4(Content_View__Debug[4]),
    .out_29(_74245_out_29), .B5(Content_View__Debug[5]), .out_31(_74245_out_31), .B6(Content_View__Debug[6]),
    .out_33(_74245_out_33), .B7(Content_View__Debug[7]), .OE(not_4_out));
  not not_5 (not_5_out, Bitmask[0]);
  not not_6 (not_6_out, Bitmask[1]);
  not not_7 (not_7_out, Bitmask[2]);
  not not_8 (not_8_out, Bitmask[3]);
  not not_9 (not_9_out, Bitmask[4]);
  not not_10 (not_10_out, Bitmask[5]);
  not not_11 (not_11_out, Bitmask[6]);
  not not_12 (not_12_out, Bitmask[7]);
  assign _74245_out_19 = not_5_out ? Content_View__Debug[0] : 1'bz;  // Controlled_Buffer controlled_buffer_19
  assign _74245_out_21 = not_6_out ? Content_View__Debug[1] : 1'bz;  // Controlled_Buffer controlled_buffer_20
  assign _74245_out_23 = not_7_out ? Content_View__Debug[2] : 1'bz;  // Controlled_Buffer controlled_buffer_21
  assign _74245_out_25 = not_8_out ? Content_View__Debug[3] : 1'bz;  // Controlled_Buffer controlled_buffer_22
  assign _74245_out_27 = not_9_out ? Content_View__Debug[4] : 1'bz;  // Controlled_Buffer controlled_buffer_23
  assign _74245_out_29 = not_10_out ? Content_View__Debug[5] : 1'bz;  // Controlled_Buffer controlled_buffer_24
  assign _74245_out_31 = not_11_out ? Content_View__Debug[6] : 1'bz;  // Controlled_Buffer controlled_buffer_25
  assign _74245_out_33 = not_12_out ? Content_View__Debug[7] : 1'bz;  // Controlled_Buffer controlled_buffer_26
  _74273_Octal_D_Flip_Flip _74273 (
    .CP(Clock__Store_data_on_rising_edge), .D0(_74245_out_19), .D1(_74245_out_21), .D2(_74245_out_23),
    .D3(_74245_out_25), .D4(_74245_out_27), .D5(_74245_out_29), .D6(_74245_out_31), .D7(_74245_out_33),
    .MR(Clears_the_register_when_0), .Q0(Content_View__Debug[0]), .Q1(Content_View__Debug[1]),
    .Q2(Content_View__Debug[2]), .Q3(Content_View__Debug[3]), .Q4(Content_View__Debug[4]),
    .Q5(Content_View__Debug[5]), .Q6(Content_View__Debug[6]), .Q7(Content_View__Debug[7]));

  // Notes on the sheet:
  //   Bus I/O 3-State Emulation
endmodule
