// Logisim project 74xx Series.circ as structural Verilog: 17 circuits, main circuit 7474 Dual-D Filp-Flop
module _7474_Dual_D_Filp_Flop (
  input  _1R,
  input  _1CP,
  input  _1D,
  input  _1S,
  input  _2R,
  input  _2CP,
  input  _2D,
  input  _2S,
  output _1Q,
  output _1NQ,
  output _2Q,
  output _2Q_2
);

  wire not_1_out, not_2_out, not_3_out, not_4_out;

  not not_1 (not_1_out, _1R);
  D_Flip_Flop d_ff_1 (.clk(_1CP), .D(_1D), .Q(_1Q), .Qn(_1NQ), .preset(not_2_out), .en(1'b1), .reset(not_1_out));
  not not_2 (not_2_out, _1S);
  not not_3 (not_3_out, _2R);
  D_Flip_Flop d_ff_2 (.clk(_2CP), .D(_2D), .Q(_2Q), .Qn(_2Q_2), .preset(not_4_out), .en(1'b1), .reset(not_3_out));
  not not_4 (not_4_out, _2S);
endmodule

module _74138_3_to_8_Line_Decoder (
  input  Enabled_when_1,
  input  Enabled_when_0,
  input  Enabled_when_0_2,
  input  Data_Select_0,
  input  Data_Select_1,
  input  Data_Select_2,
  output out_7,
  output out_8,
  output out_9,
  output out_10,
  output out_11,
  output out_12,
  output out_13,
  output out_14
);

  wire and_1_out, decoder_1_out0, decoder_1_out1, decoder_1_out2, decoder_1_out3, decoder_1_out4,
       decoder_1_out5, decoder_1_out6, decoder_1_out7, not_1_out, not_2_out;

  not not_1 (not_1_out, Enabled_when_0);
  and and_1 (and_1_out, Enabled_when_1, not_1_out, not_2_out);
  not not_2 (not_2_out, Enabled_when_0_2);
  Decoder #(.select(3)) decoder_1 (
    .out0(decoder_1_out0), .out1(decoder_1_out1), .out2(decoder_1_out2), .out3(decoder_1_out3),
    .out4(decoder_1_out4), .out5(decoder_1_out5), .out6(decoder_1_out6), .out7(decoder_1_out7),
    .sel({Data_Select_2, Data_Select_1, Data_Select_0}), .en(and_1_out));
  Pull_Resistor #(.pull(1)) pull_resistor_1 (.node(out_12));
  Pull_Resistor #(.pull(1)) pull_resistor_2 (.node(out_14));
  Pull_Resistor #(.pull(1)) pull_resistor_3 (.node(out_13));
  Pull_Resistor #(.pull(1)) pull_resistor_4 (.node(out_11));
  assign out_7 = and_1_out ? ~decoder_1_out0 : 1'bz;  // Controlled_Inverter controlled_inverter_1
  assign out_8 = and_1_out ? ~decoder_1_out1 : 1'bz;  // Controlled_Inverter controlled_inverter_2
  assign out_9 = and_1_out ? ~decoder_1_out2 : 1'bz;  // Controlled_Inverter controlled_inverter_3
  assign out_10 = and_1_out ? ~decoder_1_out3 : 1'bz;  // Controlled_Inverter controlled_inverter_4
  assign out_11 = and_1_out ? ~decoder_1_out4 : 1'bz;  // Controlled_Inverter controlled_inverter_5
  assign out_12 = and_1_out ? ~decoder_1_out5 : 1'bz;  // Controlled_Inverter controlled_inverter_6
  assign out_13 = and_1_out ? ~decoder_1_out6 : 1'bz;  // Controlled_Inverter controlled_inverter_7
  assign out_14 = and_1_out ? ~decoder_1_out7 : 1'bz;  // Controlled_Inverter controlled_inverter_8
  Pull_Resistor #(.pull(1)) pull_resistor_5 (.node(out_9));
  Pull_Resistor #(.pull(1)) pull_resistor_6 (.node(out_8));
  Pull_Resistor #(.pull(1)) pull_resistor_7 (.node(out_10));
  Pull_Resistor #(.pull(1)) pull_resistor_8 (.node(out_7));
endmodule

module _74139_Dual_2_to_4_Line_MUX (
  input  Enabled_when_0,
  input  Data_Select_0,
  input  Data_Select_1,
  input  Enabled_when_0_2,
  input  Data_Select_0_2,
  input  Data_Select_1_2,
  output out_7,
  output out_8,
  output out_9,
  output out_10,
  output out_11,
  output out_12,
  output out_13,
  output out_14
);

  wire decoder_1_out0, decoder_1_out1, decoder_1_out2, decoder_1_out3, decoder_2_out0, decoder_2_out1,
       decoder_2_out2, decoder_2_out3, not_1_out, not_2_out;

  not not_1 (not_1_out, Enabled_when_0);
  not not_2 (not_2_out, Enabled_when_0_2);
  Decoder #(.select(2)) decoder_1 (
    .out0(decoder_1_out0), .out1(decoder_1_out1), .out2(decoder_1_out2), .out3(decoder_1_out3),
    .sel({Data_Select_1, Data_Select_0}), .en(not_1_out));
  Decoder #(.select(2)) decoder_2 (
    .out0(decoder_2_out0), .out1(decoder_2_out1), .out2(decoder_2_out2), .out3(decoder_2_out3),
    .sel({Data_Select_1_2, Data_Select_0_2}), .en(not_2_out));
  Pull_Resistor #(.pull(1)) pull_resistor_1 (.node(out_8));
  Pull_Resistor #(.pull(1)) pull_resistor_2 (.node(out_9));
  Pull_Resistor #(.pull(1)) pull_resistor_3 (.node(out_10));
  assign out_7 = not_1_out ? ~decoder_1_out0 : 1'bz;  // Controlled_Inverter controlled_inverter_1
  assign out_8 = not_1_out ? ~decoder_1_out1 : 1'bz;  // Controlled_Inverter controlled_inverter_2
  assign out_9 = not_1_out ? ~decoder_1_out2 : 1'bz;  // Controlled_Inverter controlled_inverter_3
  assign out_10 = not_1_out ? ~decoder_1_out3 : 1'bz;  // Controlled_Inverter controlled_inverter_4
  Pull_Resistor #(.pull(1)) pull_resistor_4 (.node(out_14));
  Pull_Resistor #(.pull(1)) pull_resistor_5 (.node(out_13));
  Pull_Resistor #(.pull(1)) pull_resistor_6 (.node(out_12));
  assign out_11 = not_2_out ? ~decoder_2_out0 : 1'bz;  // Controlled_Inverter controlled_inverter_5
  assign out_12 = not_2_out ? ~decoder_2_out1 : 1'bz;  // Controlled_Inverter controlled_inverter_6
  assign out_13 = not_2_out ? ~decoder_2_out2 : 1'bz;  // Controlled_Inverter controlled_inverter_7
  assign out_14 = not_2_out ? ~decoder_2_out3 : 1'bz;  // Controlled_Inverter controlled_inverter_8
  Pull_Resistor #(.pull(1)) pull_resistor_7 (.node(out_7));
  Pull_Resistor #(.pull(1)) pull_resistor_8 (.node(out_11));
endmodule

module _74173_Quad_D_Flip_Flip_3S (
  input  nE1,
  input  nE2,
  input  CP,
  input  D0,
  input  MR,
  input  D1,
  input  D2,
  input  D3,
  input  nOE1,
  input  nOE2,
  output Q0,
  output Q1,
  output Q2,
  output Q3
);

  wire d_ff_1_q, d_ff_2_q, d_ff_3_q, d_ff_4_q, not_1_out, not_2_out, or_1_out, or_2_out;

  or or_1 (or_1_out, nE1, nE2);
  not not_1 (not_1_out, or_1_out);
  or or_2 (or_2_out, nOE1, nOE2);
  not not_2 (not_2_out, or_2_out);
  D_Flip_Flop d_ff_1 (.clk(CP), .D(D0), .Q(d_ff_1_q), .preset(1'b0), .en(not_1_out), .reset(MR));  // open: Qn
  D_Flip_Flop d_ff_2 (.clk(CP), .D(D1), .Q(d_ff_2_q), .preset(1'b0), .en(not_1_out), .reset(MR));  // open: Qn
  D_Flip_Flop d_ff_3 (.clk(CP), .D(D2), .Q(d_ff_3_q), .preset(1'b0), .en(not_1_out), .reset(MR));  // open: Qn
  D_Flip_Flop d_ff_4 (.clk(CP), .D(D3), .Q(d_ff_4_q), .preset(1'b0), .en(not_1_out), .reset(MR));  // open: Qn
  assign Q0 = not_2_out ? d_ff_1_q : 1'bz;  // Controlled_Buffer controlled_buffer_1
  assign Q1 = not_2_out ? d_ff_2_q : 1'bz;  // Controlled_Buffer controlled_buffer_2
  assign Q2 = not_2_out ? d_ff_3_q : 1'bz;  // Controlled_Buffer controlled_buffer_3
  assign Q3 = not_2_out ? d_ff_4_q : 1'bz;  // Controlled_Buffer controlled_buffer_4
endmodule

module _74174_Hex_D_Flip_Flop (
  input  CP,
  input  D0,
  input  D1,
  input  D2,
  input  D3,
  input  D4,
  input  D5,
  input  MR,
  output Q0,
  output Q1,
  output Q2,
  output Q3,
  output Q5,
  output Q6
);

  wire not_1_out;

  not not_1 (not_1_out, MR);
  D_Flip_Flop d_ff_1 (.clk(CP), .D(D0), .Q(Q0), .preset(1'b0), .en(1'b1), .reset(not_1_out));  // open: Qn
  D_Flip_Flop d_ff_2 (.clk(CP), .D(D1), .Q(Q1), .preset(1'b0), .en(1'b1), .reset(not_1_out));  // open: Qn
  D_Flip_Flop d_ff_3 (.clk(CP), .D(D2), .Q(Q2), .preset(1'b0), .en(1'b1), .reset(not_1_out));  // open: Qn
  D_Flip_Flop d_ff_4 (.clk(CP), .D(D3), .Q(Q3), .preset(1'b0), .en(1'b1), .reset(not_1_out));  // open: Qn
  D_Flip_Flop d_ff_5 (.clk(CP), .D(D4), .Q(Q5), .preset(1'b0), .en(1'b1), .reset(not_1_out));  // open: Qn
  D_Flip_Flop d_ff_6 (.clk(CP), .D(D5), .Q(Q6), .preset(1'b0), .en(1'b1), .reset(not_1_out));  // open: Qn
endmodule

module _74175_Quad_D_Flip_Flip (
  input  CP,
  input  D0,
  input  D1,
  input  D2,
  input  D3,
  input  MR,
  output Q0,
  output Q1,
  output Q2,
  output Q3,
  output Q0_2,
  output Q1_2,
  output Q2_2,
  output Q3_2
);

  wire not_1_out;

  not not_1 (not_1_out, MR);
  D_Flip_Flop d_ff_1 (.clk(CP), .D(D1), .Q(Q1), .Qn(Q1_2), .preset(1'b0), .en(1'b1), .reset(not_1_out));
  D_Flip_Flop d_ff_2 (.clk(CP), .D(D0), .Q(Q0), .Qn(Q0_2), .preset(1'b0), .en(1'b1), .reset(not_1_out));
  D_Flip_Flop d_ff_3 (.clk(CP), .D(D2), .Q(Q2), .Qn(Q2_2), .preset(1'b0), .en(1'b1), .reset(not_1_out));
  D_Flip_Flop d_ff_4 (.clk(CP), .D(D3), .Q(Q3), .Qn(Q3_2), .preset(1'b0), .en(1'b1), .reset(not_1_out));
endmodule

module _74243_Quad_Bus_Transceiver_3S (
  input  A0,
  input  B0,
  input  A1,
  input  B1,
  input  A2,
  input  B2,
  input  A3,
  input  B3,
  input  OEA,
  input  OEB,
  output out_11,
  output out_12,
  output out_13,
  output out_14,
  output out_15,
  output out_16,
  output out_17,
  output out_18
);

  wire and_1_out, nor_1_out;

  assign out_11 = nor_1_out ? A0 : 1'bz;  // Controlled_Buffer controlled_buffer_1
  assign out_13 = nor_1_out ? A1 : 1'bz;  // Controlled_Buffer controlled_buffer_2
  assign out_15 = nor_1_out ? A2 : 1'bz;  // Controlled_Buffer controlled_buffer_3
  assign out_17 = nor_1_out ? A3 : 1'bz;  // Controlled_Buffer controlled_buffer_4
  nor nor_1 (nor_1_out, OEA, OEB);
  assign out_12 = and_1_out ? B0 : 1'bz;  // Controlled_Buffer controlled_buffer_5
  assign out_14 = and_1_out ? B1 : 1'bz;  // Controlled_Buffer controlled_buffer_6
  assign out_16 = and_1_out ? B2 : 1'bz;  // Controlled_Buffer controlled_buffer_7
  assign out_18 = and_1_out ? B3 : 1'bz;  // Controlled_Buffer controlled_buffer_8
  and and_1 (and_1_out, OEA, OEB);
endmodule

module _74245_Octal_Bus_Transceiver_3S (
  input  A0,
  input  B0,
  input  A1,
  input  B1,
  input  A2,
  input  B2,
  input  A3,
  input  B3,
  input  A4,
  input  B4,
  input  A5,
  input  B5,
  input  A6,
  input  B6,
  input  A7,
  input  B7,
  input  DIR,
  input  OE,
  output out_19,
  output out_20,
  output out_21,
  output out_22,
  output out_23,
  output out_24,
  output out_25,
  output out_26,
  output out_27,
  output out_28,
  output out_29,
  output out_30,
  output out_31,
  output out_32,
  output out_33,
  output out_34
);

  wire and_1_out, and_2_out;

  assign out_19 = and_1_out ? A0 : 1'bz;  // Controlled_Buffer controlled_buffer_1
  assign out_21 = and_1_out ? A1 : 1'bz;  // Controlled_Buffer controlled_buffer_2
  assign out_23 = and_1_out ? A2 : 1'bz;  // Controlled_Buffer controlled_buffer_3
  assign out_25 = and_1_out ? A3 : 1'bz;  // Controlled_Buffer controlled_buffer_4
  assign out_27 = and_1_out ? A4 : 1'bz;  // Controlled_Buffer controlled_buffer_5
  assign out_29 = and_1_out ? A5 : 1'bz;  // Controlled_Buffer controlled_buffer_6
  assign out_31 = and_1_out ? A6 : 1'bz;  // Controlled_Buffer controlled_buffer_7
  assign out_33 = and_1_out ? A7 : 1'bz;  // Controlled_Buffer controlled_buffer_8
  and and_1 (and_1_out, DIR, ~OE);  // AND_Gate
  assign out_20 = and_2_out ? B0 : 1'bz;  // Controlled_Buffer controlled_buffer_9
  assign out_22 = and_2_out ? B1 : 1'bz;  // Controlled_Buffer controlled_buffer_10
  assign out_24 = and_2_out ? B2 : 1'bz;  // Controlled_Buffer controlled_buffer_11
  assign out_26 = and_2_out ? B3 : 1'bz;  // Controlled_Buffer controlled_buffer_12
  assign out_28 = and_2_out ? B4 : 1'bz;  // Controlled_Buffer controlled_buffer_13
  assign out_30 = and_2_out ? B5 : 1'bz;  // Controlled_Buffer controlled_buffer_14
  assign out_32 = and_2_out ? B6 : 1'bz;  // Controlled_Buffer controlled_buffer_15
  assign out_34 = and_2_out ? B7 : 1'bz;  // Controlled_Buffer controlled_buffer_16
  and and_2 (and_2_out, ~DIR, ~OE);  // AND_Gate
endmodule

module _74273_Octal_D_Flip_Flip (
  input  CP,
  input  D0,
  input  D1,
  input  D2,
  input  D3,
  input  D4,
  input  D5,
  input  D6,
  input  D7,
  input  MR,
  output Q0,
  output Q1,
  output Q2,
  output Q3,
  output Q4,
  output Q5,
  output Q6,
  output Q7
);

  wire not_1_out;

  not not_1 (not_1_out, MR);
  Register register_1 (
    .D({D7, D6, D5, D4, D3, D2, D1, D0}), .Q({Q7, Q6, Q5, Q4, Q3, Q2, Q1, Q0}), .clk(CP), .clr(not_1_out));  // open: en
endmodule

module _74373_Octal_D_Latch_3S (
  input  _1D,
  input  _2D,
  input  _3D,
  input  _4D,
  input  _5D,
  input  _6D,
  input  _7D,
  input  _8D,
  input  Load_data_when_1,
  input  Output_enabled_when_0,
  output _1Q,
  output _2Q,
  output _3Q,
  output _4Q,
  output _5Q,
  output _6Q,
  output _7Q,
  output _8Q
);

  wire nand_1_out, nand_2_out, nand_3_out, nand_4_out, nand_5_out, nand_6_out, nand_7_out, nand_8_out,
       nand_9_out, nand_10_out, nand_11_out, nand_12_out, nand_13_out, nand_14_out, nand_15_out, nand_16_out,
       nand_17_out, nand_18_out, nand_19_out, nand_20_out, nand_21_out, nand_22_out, nand_23_out,
       nand_24_out, nand_25_out, nand_26_out, nand_27_out, nand_28_out, nand_29_out, nand_30_out,
       nand_31_out, nand_32_out, not_1_out;

  not not_1 (not_1_out, Output_enabled_when_0);
  nand nand_1 (nand_1_out, _1D, Load_data_when_1);
  nand nand_2 (nand_2_out, nand_1_out, Load_data_when_1);
  nand nand_3 (nand_3_out, _2D, Load_data_when_1);
  nand nand_4 (nand_4_out, nand_3_out, Load_data_when_1);
  nand nand_5 (nand_5_out, _3D, Load_data_when_1);
  nand nand_6 (nand_6_out, nand_5_out, Load_data_when_1);
  nand nand_7 (nand_7_out, _4D, Load_data_when_1);
  nand nand_8 (nand_8_out, nand_7_out, Load_data_when_1);
  nand nand_9 (nand_9_out, _5D, Load_data_when_1);
  nand nand_10 (nand_10_out, nand_9_out, Load_data_when_1);
  nand nand_11 (nand_11_out, _6D, Load_data_when_1);
  nand nand_12 (nand_12_out, nand_11_out, Load_data_when_1);
  nand nand_13 (nand_13_out, _7D, Load_data_when_1);
  nand nand_14 (nand_14_out, nand_13_out, Load_data_when_1);
  nand nand_15 (nand_15_out, _8D, Load_data_when_1);
  nand nand_16 (nand_16_out, nand_15_out, Load_data_when_1);
  assign _1Q = not_1_out ? nand_17_out : 1'bz;  // Controlled_Buffer controlled_buffer_1
  nand nand_17 (nand_17_out, nand_1_out, nand_18_out);
  nand nand_18 (nand_18_out, nand_17_out, nand_2_out);
  nand nand_19 (nand_19_out, nand_3_out, nand_20_out);
  assign _2Q = not_1_out ? nand_19_out : 1'bz;  // Controlled_Buffer controlled_buffer_2
  nand nand_20 (nand_20_out, nand_19_out, nand_4_out);
  assign _3Q = not_1_out ? nand_21_out : 1'bz;  // Controlled_Buffer controlled_buffer_3
  nand nand_21 (nand_21_out, nand_5_out, nand_22_out);
  nand nand_22 (nand_22_out, nand_21_out, nand_6_out);
  nand nand_23 (nand_23_out, nand_7_out, nand_24_out);
  assign _4Q = not_1_out ? nand_23_out : 1'bz;  // Controlled_Buffer controlled_buffer_4
  nand nand_24 (nand_24_out, nand_23_out, nand_8_out);
  nand nand_25 (nand_25_out, nand_9_out, nand_26_out);
  assign _5Q = not_1_out ? nand_25_out : 1'bz;  // Controlled_Buffer controlled_buffer_5
  nand nand_26 (nand_26_out, nand_25_out, nand_10_out);
  assign _6Q = not_1_out ? nand_27_out : 1'bz;  // Controlled_Buffer controlled_buffer_6
  nand nand_27 (nand_27_out, nand_11_out, nand_28_out);
  nand nand_28 (nand_28_out, nand_27_out, nand_12_out);
  assign _7Q = not_1_out ? nand_29_out : 1'bz;  // Controlled_Buffer controlled_buffer_7
  nand nand_29 (nand_29_out, nand_13_out, nand_30_out);
  nand nand_30 (nand_30_out, nand_29_out, nand_14_out);
  nand nand_31 (nand_31_out, nand_15_out, nand_32_out);
  assign _8Q = not_1_out ? nand_31_out : 1'bz;  // Controlled_Buffer controlled_buffer_8
  nand nand_32 (nand_32_out, nand_31_out, nand_16_out);
endmodule

module _74374_Octal_D_Flip_Flip_3S (
  input  CP,
  input  D0,
  input  D1,
  input  D2,
  input  D3,
  input  D4,
  input  D5,
  input  D6,
  input  D7,
  input  OE,
  output Q0,
  output Q1,
  output Q2,
  output Q3,
  output Q4,
  output Q5,
  output Q6,
  output Q7
);

  wire not_1_out;
  wire [7:0] register_1_q;

  not not_1 (not_1_out, OE);
  Register register_1 (.D({D7, D6, D5, D4, D3, D2, D1, D0}), .en(1'b1), .Q(register_1_q), .clk(CP), .clr(1'b0));
  assign Q0 = not_1_out ? register_1_q[0] : 1'bz;  // Controlled_Buffer controlled_buffer_1
  assign Q1 = not_1_out ? register_1_q[1] : 1'bz;  // Controlled_Buffer controlled_buffer_2
  assign Q2 = not_1_out ? register_1_q[2] : 1'bz;  // Controlled_Buffer controlled_buffer_3
  assign Q3 = not_1_out ? register_1_q[3] : 1'bz;  // Controlled_Buffer controlled_buffer_4
  assign Q4 = not_1_out ? register_1_q[4] : 1'bz;  // Controlled_Buffer controlled_buffer_5
  assign Q5 = not_1_out ? register_1_q[5] : 1'bz;  // Controlled_Buffer controlled_buffer_6
  assign Q6 = not_1_out ? register_1_q[6] : 1'bz;  // Controlled_Buffer controlled_buffer_7
  assign Q7 = not_1_out ? register_1_q[7] : 1'bz;  // Controlled_Buffer controlled_buffer_8
endmodule

module _74377_Octal_D_Flip_Flip (
  input  D0,
  input  D1,
  input  D2,
  input  D3,
  input  E,
  input  CP,
  input  D4,
  input  D5,
  input  D6,
  input  D7,
  output Q0,
  output Q1,
  output Q2,
  output Q3,
  output Q4,
  output Q5,
  output Q6,
  output Q7
);

  wire and_1_out, and_2_out, and_3_out, and_4_out, and_5_out, and_6_out, and_7_out, and_8_out, and_9_out,
       and_10_out, and_11_out, and_12_out, and_13_out, and_14_out, and_15_out, and_16_out, not_1_out,
       or_1_out, or_2_out, or_3_out, or_4_out, or_5_out, or_6_out, or_7_out, or_8_out;

  not not_1 (not_1_out, E);
  and and_1 (and_1_out, ~not_1_out, Q3);  // AND_Gate
  and and_2 (and_2_out, not_1_out, D3);
  or or_1 (or_1_out, and_2_out, and_1_out);
  and and_3 (and_3_out, ~not_1_out, Q7);  // AND_Gate
  and and_4 (and_4_out, not_1_out, D7);
  or or_2 (or_2_out, and_4_out, and_3_out);
  and and_5 (and_5_out, not_1_out, D2);
  D_Flip_Flop d_ff_1 (.clk(CP), .D(or_1_out), .Q(Q3), .preset(1'b0), .en(1'b1), .reset(1'b0));  // open: Qn
  and and_6 (and_6_out, not_1_out, D6);
  D_Flip_Flop d_ff_2 (.clk(CP), .D(or_2_out), .Q(Q7), .preset(1'b0), .en(1'b1), .reset(1'b0));  // open: Qn
  and and_7 (and_7_out, ~not_1_out, Q2);  // AND_Gate
  or or_3 (or_3_out, and_5_out, and_7_out);
  D_Flip_Flop d_ff_3 (.clk(CP), .D(or_3_out), .Q(Q2), .preset(1'b0), .en(1'b1), .reset(1'b0));  // open: Qn
  and and_8 (and_8_out, ~not_1_out, Q6);  // AND_Gate
  or or_4 (or_4_out, and_6_out, and_8_out);
  D_Flip_Flop d_ff_4 (.clk(CP), .D(or_4_out), .Q(Q6), .preset(1'b0), .en(1'b1), .reset(1'b0));  // open: Qn
  and and_9 (and_9_out, ~not_1_out, Q1);  // AND_Gate
  and and_10 (and_10_out, not_1_out, D1);
  or or_5 (or_5_out, and_10_out, and_9_out);
  and and_11 (and_11_out, ~not_1_out, Q5);  // AND_Gate
  and and_12 (and_12_out, not_1_out, D5);
  or or_6 (or_6_out, and_12_out, and_11_out);
  and and_13 (and_13_out, not_1_out, D0);
  D_Flip_Flop d_ff_5 (.clk(CP), .D(or_5_out), .Q(Q1), .preset(1'b0), .en(1'b1), .reset(1'b0));  // open: Qn
  and and_14 (and_14_out, not_1_out, D4);
  D_Flip_Flop d_ff_6 (.clk(CP), .D(or_6_out), .Q(Q5), .preset(1'b0), .en(1'b1), .reset(1'b0));  // open: Qn
  and and_15 (and_15_out, ~not_1_out, Q0);  // AND_Gate
  or or_7 (or_7_out, and_13_out, and_15_out);
  D_Flip_Flop d_ff_7 (.clk(CP), .D(or_7_out), .Q(Q0), .preset(1'b0), .en(1'b1), .reset(1'b0));  // open: Qn
  and and_16 (and_16_out, ~not_1_out, Q4);  // AND_Gate
  or or_8 (or_8_out, and_14_out, and_16_out);
  D_Flip_Flop d_ff_8 (.clk(CP), .D(or_8_out), .Q(Q4), .preset(1'b0), .en(1'b1), .reset(1'b0));  // open: Qn
endmodule

module _74534_Octal_D_FlipFlip_3S (
  input  CP,
  input  D0,
  input  D1,
  input  D2,
  input  D3,
  input  D4,
  input  D5,
  input  D6,
  input  D7,
  input  OE,
  output Q0,
  output Q1,
  output Q2,
  output Q3,
  output Q4,
  output Q5,
  output Q6,
  output Q7
);

  wire not_1_out;
  wire [7:0] register_1_q;

  not not_1 (not_1_out, OE);
  Register register_1 (.D({D7, D6, D5, D4, D3, D2, D1, D0}), .en(1'b1), .Q(register_1_q), .clk(CP), .clr(1'b0));
  assign Q0 = not_1_out ? register_1_q[0] : 1'bz;  // Controlled_Buffer controlled_buffer_1
  assign Q1 = not_1_out ? register_1_q[1] : 1'bz;  // Controlled_Buffer controlled_buffer_2
  assign Q2 = not_1_out ? register_1_q[2] : 1'bz;  // Controlled_Buffer controlled_buffer_3
  assign Q3 = not_1_out ? register_1_q[3] : 1'bz;  // Controlled_Buffer controlled_buffer_4
  assign Q4 = not_1_out ? register_1_q[4] : 1'bz;  // Controlled_Buffer controlled_buffer_5
  assign Q5 = not_1_out ? register_1_q[5] : 1'bz;  // Controlled_Buffer controlled_buffer_6
  assign Q6 = not_1_out ? register_1_q[6] : 1'bz;  // Controlled_Buffer controlled_buffer_7
  assign Q7 = not_1_out ? register_1_q[7] : 1'bz;  // Controlled_Buffer controlled_buffer_8
endmodule

module _74564_Octal_D_FlipFlip_3S (
  input  CP,
  input  D0,
  input  D1,
  input  D2,
  input  D3,
  input  D4,
  input  D5,
  input  D6,
  input  D7,
  input  OE,
  output Q0,
  output Q1,
  output Q2,
  output Q3,
  output Q4,
  output Q5,
  output Q6,
  output Q7
);

  wire d_ff_1_q, d_ff_2_q, d_ff_3_q, d_ff_4_q, d_ff_5_q, d_ff_6_q, d_ff_7_q, d_ff_8_q, not_1_out;

  not not_1 (not_1_out, OE);
  D_Flip_Flop d_ff_1 (.clk(CP), .D(D0), .Q(d_ff_1_q), .preset(1'b0), .en(1'b1), .reset(1'b0));  // open: Qn
  D_Flip_Flop d_ff_2 (.clk(CP), .D(D1), .Q(d_ff_2_q), .preset(1'b0), .en(1'b1), .reset(1'b0));  // open: Qn
  D_Flip_Flop d_ff_3 (.clk(CP), .D(D2), .Q(d_ff_3_q), .preset(1'b0), .en(1'b1), .reset(1'b0));  // open: Qn
  D_Flip_Flop d_ff_4 (.clk(CP), .D(D3), .Q(d_ff_4_q), .preset(1'b0), .en(1'b1), .reset(1'b0));  // open: Qn
  D_Flip_Flop d_ff_5 (.clk(CP), .D(D5), .Q(d_ff_5_q), .preset(1'b0), .en(1'b1), .reset(1'b0));  // open: Qn
  D_Flip_Flop d_ff_6 (.clk(CP), .D(D4), .Q(d_ff_6_q), .preset(1'b0), .en(1'b1), .reset(1'b0));  // open: Qn
  D_Flip_Flop d_ff_7 (.clk(CP), .D(D6), .Q(d_ff_7_q), .preset(1'b0), .en(1'b1), .reset(1'b0));  // open: Qn
  D_Flip_Flop d_ff_8 (.clk(CP), .D(D7), .Q(d_ff_8_q), .preset(1'b0), .en(1'b1), .reset(1'b0));  // open: Qn
  assign Q0 = not_1_out ? ~d_ff_1_q : 1'bz;  // Controlled_Inverter controlled_inverter_1
  assign Q1 = not_1_out ? ~d_ff_2_q : 1'bz;  // Controlled_Inverter controlled_inverter_2
  assign Q2 = not_1_out ? ~d_ff_3_q : 1'bz;  // Controlled_Inverter controlled_inverter_3
  assign Q3 = not_1_out ? ~d_ff_4_q : 1'bz;  // Controlled_Inverter controlled_inverter_4
  assign Q4 = not_1_out ? ~d_ff_6_q : 1'bz;  // Controlled_Inverter controlled_inverter_5
  assign Q5 = not_1_out ? ~d_ff_5_q : 1'bz;  // Controlled_Inverter controlled_inverter_6
  assign Q6 = not_1_out ? ~d_ff_7_q : 1'bz;  // Controlled_Inverter controlled_inverter_7
  assign Q7 = not_1_out ? ~d_ff_8_q : 1'bz;  // Controlled_Inverter controlled_inverter_8
endmodule

module _74574_Octal_D_Flip_Flip_3S (
  input  CP,
  input  D0,
  input  D1,
  input  D2,
  input  D3,
  input  D4,
  input  D5,
  input  D6,
  input  D7,
  input  OE,
  output Q0,
  output Q1,
  output Q2,
  output Q3,
  output Q4,
  output Q5,
  output Q6,
  output Q7
);

  wire d_ff_1_q, d_ff_2_q, d_ff_3_q, d_ff_4_q, d_ff_5_q, d_ff_6_q, d_ff_7_q, d_ff_8_q, not_1_out;

  not not_1 (not_1_out, OE);
  D_Flip_Flop d_ff_1 (.clk(CP), .D(D0), .Q(d_ff_1_q), .preset(1'b0), .en(1'b1), .reset(1'b0));  // open: Qn
  D_Flip_Flop d_ff_2 (.clk(CP), .D(D1), .Q(d_ff_2_q), .preset(1'b0), .en(1'b1), .reset(1'b0));  // open: Qn
  D_Flip_Flop d_ff_3 (.clk(CP), .D(D2), .Q(d_ff_3_q), .preset(1'b0), .en(1'b1), .reset(1'b0));  // open: Qn
  D_Flip_Flop d_ff_4 (.clk(CP), .D(D3), .Q(d_ff_4_q), .preset(1'b0), .en(1'b1), .reset(1'b0));  // open: Qn
  D_Flip_Flop d_ff_5 (.clk(CP), .D(D4), .Q(d_ff_5_q), .preset(1'b0), .en(1'b1), .reset(1'b0));  // open: Qn
  D_Flip_Flop d_ff_6 (.clk(CP), .D(D5), .Q(d_ff_6_q), .preset(1'b0), .en(1'b1), .reset(1'b0));  // open: Qn
  D_Flip_Flop d_ff_7 (.clk(CP), .D(D6), .Q(d_ff_7_q), .preset(1'b0), .en(1'b1), .reset(1'b0));  // open: Qn
  D_Flip_Flop d_ff_8 (.clk(CP), .D(D7), .Q(d_ff_8_q), .preset(1'b0), .en(1'b1), .reset(1'b0));  // open: Qn
  assign Q0 = not_1_out ? d_ff_1_q : 1'bz;  // Controlled_Buffer controlled_buffer_1
  assign Q1 = not_1_out ? d_ff_2_q : 1'bz;  // Controlled_Buffer controlled_buffer_2
  assign Q2 = not_1_out ? d_ff_3_q : 1'bz;  // Controlled_Buffer controlled_buffer_3
  assign Q3 = not_1_out ? d_ff_4_q : 1'bz;  // Controlled_Buffer controlled_buffer_4
  assign Q4 = not_1_out ? d_ff_5_q : 1'bz;  // Controlled_Buffer controlled_buffer_5
  assign Q5 = not_1_out ? d_ff_6_q : 1'bz;  // Controlled_Buffer controlled_buffer_6
  assign Q6 = not_1_out ? d_ff_7_q : 1'bz;  // Controlled_Buffer controlled_buffer_7
  assign Q7 = not_1_out ? d_ff_8_q : 1'bz;  // Controlled_Buffer controlled_buffer_8
endmodule

module _74623_Octal_Bus_Transceiver_3S (
  input  A0,
  input  B0,
  input  A1,
  input  B1,
  input  A2,
  input  B2,
  input  A3,
  input  B3,
  input  A4,
  input  B4,
  input  A5,
  input  B5,
  input  A6,
  input  B6,
  input  A7,
  input  B7,
  input  OEAB,
  input  OEBA,
  output out_19,
  output out_20,
  output out_21,
  output out_22,
  output out_23,
  output out_24,
  output out_25,
  output out_26,
  output out_27,
  output out_28,
  output out_29,
  output out_30,
  output out_31,
  output out_32,
  output out_33,
  output out_34
);

  wire not_1_out;

  assign out_19 = OEAB ? A0 : 1'bz;  // Controlled_Buffer controlled_buffer_1
  assign out_21 = OEAB ? A1 : 1'bz;  // Controlled_Buffer controlled_buffer_2
  assign out_23 = OEAB ? A2 : 1'bz;  // Controlled_Buffer controlled_buffer_3
  assign out_25 = OEAB ? A3 : 1'bz;  // Controlled_Buffer controlled_buffer_4
  assign out_27 = OEAB ? A4 : 1'bz;  // Controlled_Buffer controlled_buffer_5
  assign out_29 = OEAB ? A5 : 1'bz;  // Controlled_Buffer controlled_buffer_6
  assign out_31 = OEAB ? A6 : 1'bz;  // Controlled_Buffer controlled_buffer_7
  assign out_33 = OEAB ? A7 : 1'bz;  // Controlled_Buffer controlled_buffer_8
  assign out_20 = not_1_out ? B0 : 1'bz;  // Controlled_Buffer controlled_buffer_9
  assign out_22 = not_1_out ? B1 : 1'bz;  // Controlled_Buffer controlled_buffer_10
  assign out_24 = not_1_out ? B2 : 1'bz;  // Controlled_Buffer controlled_buffer_11
  assign out_26 = not_1_out ? B3 : 1'bz;  // Controlled_Buffer controlled_buffer_12
  assign out_28 = not_1_out ? B4 : 1'bz;  // Controlled_Buffer controlled_buffer_13
  assign out_30 = not_1_out ? B5 : 1'bz;  // Controlled_Buffer controlled_buffer_14
  assign out_32 = not_1_out ? B6 : 1'bz;  // Controlled_Buffer controlled_buffer_15
  assign out_34 = not_1_out ? B7 : 1'bz;  // Controlled_Buffer controlled_buffer_16
  not not_1 (not_1_out, OEBA);
endmodule

module _744020_14_Stage_Binary_Counter (
  input  Clock__Count_on_falling_edge,
  input  Master_Reset,
  output out_3,
  output out_4,
  output out_5,
  output out_6,
  output out_7,
  output out_8,
  output out_9,
  output out_10,
  output out_11,
  output out_12,
  output out_13,
  output out_14,
  output out_15,
  output out_16
);

  wire not_1_out;

  not not_1 (not_1_out, Clock__Count_on_falling_edge);
  Counter #(.width(14), .max('h3fff)) counter_1 (
    .load(1'b0), .count(1'b1),
    .Q({out_16, out_15, out_14, out_13, out_12, out_11, out_10, out_9, out_8, out_7, out_6, out_5, out_4, out_3}),
    .clk(not_1_out), .clr(Master_Reset));  // open: D, carry
endmodule
